// Logisim project cpu24.circ as structural Verilog: 16 circuits, main circuit ◇重定向流水线
module \单周期MIPS  (
);

  wire and_1_out, and_2_out, and_3_out, and_4_out, and_5_out, and_6_out, and_7_out, BGEZ, Branch, CLK,
       comparator_1_eq, Go, JAL, JMP, JR, LHU, mips_alu_1_equal, not_1_out, or_1_out, RST, SignedExt, SLTIU,
       SRAV, Syscall, \暂停 , \硬布线控制器_1_alu_src , \硬布线控制器_1_beq , \硬布线控制器_1_bne , \硬布线控制器_1_memtoreg ,
       \硬布线控制器_1_memwrite , \硬布线控制器_1_regdst , \硬布线控制器_1_regwrite ;
  wire [3:0] \硬布线控制器_1_alu_op ;
  wire [4:0] multiplexer_3_out, multiplexer_4_out, multiplexer_5_out, multiplexer_7_out, multiplexer_10_out;
  wire [15:0] \总周期数 , \无条件分支数 , \条件分支成功数 ;
  wire [25:0] instr_index;
  wire [31:0] ALU_Result, bit_extender_1_out, bit_extender_2_out, Din, LedData, MemData, multiplexer_1_out,
       multiplexer_6_out, multiplexer_8_out, multiplexer_9_out, multiplexer_12_out, multiplexer_13_out, PC_4,
       PC_q, R1, R2, ram_1_data, shifter_1_out, \无条件跳转地址 , \条件分支跳转地址 ;
  wire [31:26] rom_1_data;

  Button \u_总复位  (.out(RST));
  Button \u_继续运行  (.out(Go));
  Clock clock_1 (.out(CLK));
  Hex_Digit_Display hex_digit_display_1 (.value(LedData[27:24]));  // open: dp
  Hex_Digit_Display hex_digit_display_2 (.value(LedData[31:28]));  // open: dp
  Hex_Digit_Display hex_digit_display_3 (.value(LedData[19:16]));  // open: dp
  Hex_Digit_Display hex_digit_display_4 (.value(LedData[23:20]));  // open: dp
  Hex_Digit_Display hex_digit_display_5 (.value(LedData[11:8]));  // open: dp
  Hex_Digit_Display hex_digit_display_6 (.value(LedData[15:12]));  // open: dp
  Multiplexer #(.select(2), .width(32), .enable("false")) multiplexer_1 (
    .in0(PC_4), .in1(\无条件跳转地址 ), .in2(\条件分支跳转地址 ), .in3({32{1'b0}}), .out(multiplexer_1_out),
    .sel({Branch, JMP}));
  Hex_Digit_Display hex_digit_display_7 (.value(LedData[7:4]));  // open: dp
  Hex_Digit_Display hex_digit_display_8 (.value(LedData[3:0]));  // open: dp
  Register #(.width(32)) PC (.D(multiplexer_1_out), .en(\暂停 ), .Q(PC_q), .clk(CLK), .clr(RST));
  Adder #(.width(32)) adder_1 (.a(PC_q), .b(32'h4), .out(PC_4));  // open: cin, cout
  ROM #(.addrWidth(10), .dataWidth(32)) rom_1 (.addr(PC_q[11:2]), .data({rom_1_data, instr_index}));  // open: sel
  Counter #(.width(16), .max('hffff)) counter_1 (
    .count(\暂停 ), .Q(\总周期数 ), .clk(CLK), .clr(RST));  // open: load, D, carry
  // Probe on \总周期数 
  // Probe on \无条件分支数 
  // Probe on \条件分支成功数 
  Multiplexer #(.width(32), .enable("false")) multiplexer_2 (
    .in0({PC_4[31:28], instr_index, 2'b00}), .in1(R1), .out(\无条件跳转地址 ), .sel(JR));
  \硬布线控制器  \u_硬布线控制器_1  (
    .Func(instr_index[5:0]), .OP(rom_1_data), .ALU_OP(\硬布线控制器_1_alu_op ), .MemToReg(\硬布线控制器_1_memtoreg ),
    .MemWrite(\硬布线控制器_1_memwrite ), .ALU_SRC(\硬布线控制器_1_alu_src ), .RegWrite(\硬布线控制器_1_regwrite ),
    .SysCALL(Syscall), .SignedExt(SignedExt), .RegDst(\硬布线控制器_1_regdst ), .JR(JR), .JMP(JMP),
    .Beq(\硬布线控制器_1_beq ), .JAL(JAL), .Bne(\硬布线控制器_1_bne ), .LHU(LHU), .BGEZ(BGEZ), .SLTIU(SLTIU), .SRAV(SRAV));
  Multiplexer #(.width(5), .enable("false")) multiplexer_3 (
    .in0(instr_index[25:21]), .in1(5'b00010), .out(multiplexer_3_out), .sel(Syscall));
  Multiplexer #(.width(5), .enable("false")) multiplexer_4 (
    .in0(instr_index[20:16]), .in1(5'b00100), .out(multiplexer_4_out), .sel(Syscall));
  assign bit_extender_1_out = {{16{1'b0}}, instr_index[15:0]};  // Bit_Extender bit_extender_1
  assign bit_extender_2_out = {{16{instr_index[15]}}, instr_index[15:0]};  // Bit_Extender bit_extender_2
  Multiplexer #(.width(5), .enable("false")) multiplexer_5 (
    .in0(instr_index[20:16]), .in1(instr_index[15:11]), .out(multiplexer_5_out), .sel(\硬布线控制器_1_regdst ));
  Multiplexer #(.width(32), .enable("false")) multiplexer_6 (
    .in0(bit_extender_1_out), .in1(bit_extender_2_out), .out(multiplexer_6_out), .sel(SignedExt));
  Shifter #(.width(32)) shifter_1 (.in(bit_extender_2_out), .\dist (5'b00010), .out(shifter_1_out));
  Multiplexer #(.width(5), .enable("false")) multiplexer_7 (
    .in0(multiplexer_5_out), .in1({5{1'b1}}), .out(multiplexer_7_out), .sel(JAL));
  and and_1 (and_1_out, Branch, \暂停 );
  Multiplexer #(.width(32), .enable("false")) multiplexer_8 (
    .in0(multiplexer_6_out), .in1({32{1'b0}}), .out(multiplexer_8_out), .sel(BGEZ));
  Comparator #(.width(32)) comparator_1 (.a(R1), .b(32'h22), .eq(comparator_1_eq));  // open: gt, lt
  Counter #(.width(16), .max('hffff)) counter_2 (
    .count(and_1_out), .Q(\条件分支成功数 ), .clk(CLK), .clr(RST));  // open: load, D, carry
  MIPS_Regifile mips_regifile_1 (
    .Din(Din), .Clk(CLK), .R1(R1), .R2(R2), .WE(\硬布线控制器_1_regwrite ), .W_num(multiplexer_7_out),
    .R1_num(multiplexer_3_out), .R2_num(multiplexer_4_out));
  Adder #(.width(32)) adder_2 (.a(shifter_1_out), .b(PC_4), .out(\条件分支跳转地址 ));  // open: cin, cout
  and and_2 (and_2_out, comparator_1_eq, Syscall);
  and and_3 (and_3_out, ~comparator_1_eq, Syscall);  // AND_Gate
  Multiplexer #(.width(32), .enable("false")) multiplexer_9 (
    .in0(R2), .in1(multiplexer_8_out), .out(multiplexer_9_out), .sel(\硬布线控制器_1_alu_src ));
  Multiplexer #(.width(5), .enable("false")) multiplexer_10 (
    .in0(instr_index[10:6]), .in1(R1[4:0]), .out(multiplexer_10_out), .sel(SRAV));
  Register #(.width(32)) register_1 (.D(R2), .en(and_2_out), .Q(LedData), .clk(CLK), .clr(RST));
  D_Flip_Flop d_ff_1 (.clk(CLK), .D(and_3_out), .Qn(\暂停 ), .preset(1'b0), .en(\暂停 ), .reset(or_1_out));  // open: Q
  or or_1 (or_1_out, RST, Go);
  and and_4 (and_4_out, \硬布线控制器_1_beq , mips_alu_1_equal);
  MIPS_ALU mips_alu_1 (
    .X(R1), .Y(multiplexer_9_out), .AluOP(\硬布线控制器_1_alu_op ), .Equal(mips_alu_1_equal), .Result(ALU_Result),
    .shamt(multiplexer_10_out));  // open: Result_2
  and and_5 (and_5_out, JMP, \暂停 );
  and and_6 (and_6_out, BGEZ, ~ALU_Result[0]);  // AND_Gate
  or or_2 (Branch, and_4_out, and_6_out, and_7_out);
  and and_7 (and_7_out, \硬布线控制器_1_bne , ~mips_alu_1_equal);  // AND_Gate
  Counter #(.width(16), .max('hffff)) counter_3 (
    .count(and_5_out), .Q(\无条件分支数 ), .clk(CLK), .clr(RST));  // open: load, D, carry
  not not_1 (not_1_out, \硬布线控制器_1_memwrite );
  Multiplexer #(.width(32), .enable("false")) multiplexer_11 (
    .in0(ALU_Result), .in1(ram_1_data), .out(MemData), .sel(\硬布线控制器_1_memtoreg ));
  RAM #(.addrWidth(10), .dataWidth(32), .bus("separate")) ram_1 (
    .addr(ALU_Result[11:2]), .din(R2), .data(ram_1_data), .str(\硬布线控制器_1_memwrite ), .clk(CLK),
    .ld(not_1_out), .clr(RST));  // open: sel
  Multiplexer #(.width(32), .enable("false")) multiplexer_12 (
    .in0(MemData), .in1(PC_4), .out(multiplexer_12_out), .sel(JAL));
  Multiplexer #(.width(32), .enable("false")) multiplexer_13 (
    .in0({{16{1'b0}}, MemData[15:0]}), .in1({{16{1'b0}}, MemData[31:16]}), .out(multiplexer_13_out),
    .sel(ALU_Result[1]));
  Multiplexer #(.select(2), .width(32), .enable("false")) multiplexer_14 (
    .in0(multiplexer_12_out), .in1(ALU_Result), .in2(multiplexer_13_out), .in3({32{1'b0}}), .out(Din),
    .sel({LHU, SLTIU}));

  // Other names for the same wires on the sheet: PCSel[1:0] = {Branch, JMP}

  // Notes on the sheet:
  //   数码管输出应该用寄存器锁存，否则显示数据只能一闪而过
  //   可以通过项目增加Logisim库的方式将前几次实验完成的电路作为子电路引入到本电路中使用
  //   数码管输出
  //   总复位信号应将除ROM以外所有存储组件全部清零
  //   指令存储器
  //   contents of rom_1 (hex, n*v repeats v):
  //   20110001 8100005 20110001 20120002 20130003 8100009 20110001 20120002 20130003 810000d 20110001
  //   20120002 20130003 8100011 20110001 20120002 20130003 c1000f6 20100001 20110001 118fc0 112020
  //   20020022 c 118882 12200001 8100015 112020 20020022 c 20110001 118880 112020 20020022 c 12200001
  //   810001f 20110001 118fc0 112020 20020022 c 1188c3 112020 20020022 c 118903 112020 20020022 c 118903
  //   112020 20020022 c 118903 112020 20020022 c 118903 112020 20020022 c 118903 112020 20020022 c 118903
  //   112020 20020022 c 118903 112020 20020022 c 20100001 109fc0 139fc3 8021 2012000c 24160003 26100001
  //   3210000f 20080008 20090001 139900 2709825 132020 20020022 c 1094022 1500fff9 22100001 2018000f
  //   2188024 108700 20080008 20090001 139902 2709825 132021 20020022 c 1094022 1500fff9 108702 2c9b022
  //   12c00001 8100050 4020 1084027 84400 3508ffff 82021 20020022 c 2010ffff 20110000 ae300000 22100001
  //   22310004 ae300000 22100001 22310004 ae300000 22100001 22310004 ae300000 22100001 22310004 ae300000
  //   22100001 22310004 ae300000 22100001 22310004 ae300000 22100001 22310004 ae300000 22100001 22310004
  //   ae300000 22100001 22310004 ae300000 22100001 22310004 ae300000 22100001 22310004 ae300000 22100001
  //   22310004 ae300000 22100001 22310004 ae300000 22100001 22310004 ae300000 22100001 22310004 ae300000
  //   22100001 22310004 22100001 8020 2011003c 8e130000 8e340000 274402a 11000002 ae330000 ae140000
  //   2231fffc 1611fff8 102020 20020022 c 22100004 2011003c 1611fff2 20020032 c 20080001 20090003 20110876
  //   118d00 112020 20020022 c 200b0008 1118807 1318807 112020 20020022 c 216bffff 1560fff9 2002000a c
  //   2008ffff 20090000 20111997 112020 20020022 c 2288820 2e291949 1120fffa 2002000a c 20090000 200b0010
  //   34118483 20120404 118c00 129400 36318281 22520404 ad310000 2328820 21290004 216bffff 1560fffb
  //   200b0020 20090000 95310000 112020 20020022 c 21290002 216bffff 1560fff9 2002000a c 2011000f 112020
  //   20020022 c 2231ffff 621fffb 2002000a c 2002000a c 20100000 22100001 102020 20020022 c 22100002
  //   102020 20020022 c 22100003 102020 20020022 c 22100004 102020 20020022 c 22100005 102020 20020022 c
  //   22100006 102020 20020022 c 22100007 102020 20020022 c 22100008 102020 20020022 20020022 c 3e00008
  //   SLTIU
  //   LHU
  //   BGEZ
  //   OP
  //   Func
  //   rs
  //   指令字
  //   rt
  //   rd
  //   imm
  //   shamt
  //   Beq
  //   JMP
  //   JR
  //   Bne
  //   SRAV
  //   OP
  //   JAL
  //   Func
  //   Syscall
  //   MemToReg
  //   MemWrite
  //   AluOP
  //   AluSrcB
  //   RegWrite
  //   RegDst
endmodule

// 单周期硬布线控制器
module \硬布线控制器  (
  input  [5:0] OP,
  input  [5:0] Func,
  output [3:0] ALU_OP,
  output MemToReg,
  output MemWrite,
  output ALU_SRC,
  output RegWrite,
  output SysCALL,
  output SignedExt,
  output RegDst,
  output Beq,
  output Bne,
  output JR,
  output JMP,
  output JAL,
  output SRAV,
  output SLTIU,
  output LHU,
  output BGEZ
);

  wire comparator_1_eq, comparator_5_eq;

  Comparator #(.width(6), .mode("unsigned")) comparator_1 (
    .a(OP), .b({6{1'b0}}), .eq(comparator_1_eq));  // open: gt, lt
  Comparator #(.width(6), .mode("unsigned")) comparator_2 (.a(OP), .b(6'b001011), .eq(SLTIU));  // open: gt, lt
  Comparator #(.width(6), .mode("unsigned")) comparator_3 (.a(OP), .b(6'b100101), .eq(LHU));  // open: gt, lt
  Comparator #(.width(6), .mode("unsigned")) comparator_4 (.a(OP), .b(6'b000001), .eq(BGEZ));  // open: gt, lt
  \运算控制器  \u_运算控制器_1  (
    .OP0(OP[0]), .OP1(OP[1]), .OP2(OP[2]), .OP3(OP[3]), .OP4(OP[4]), .OP5(OP[5]), .F0(Func[0]), .F1(Func[1]),
    .F2(Func[2]), .F3(Func[3]), .F4(Func[4]), .F5(Func[5]), .S0(ALU_OP[0]), .S1(ALU_OP[1]), .S2(ALU_OP[2]),
    .S3(ALU_OP[3]));
  \控制信号生成  \u_控制信号生成_1  (
    .OP0(OP[0]), .OP1(OP[1]), .OP2(OP[2]), .OP3(OP[3]), .OP4(OP[4]), .OP5(OP[5]), .F0(Func[0]), .F1(Func[1]),
    .F2(Func[2]), .F3(Func[3]), .F4(Func[4]), .F5(Func[5]), .MemToReg(MemToReg), .MemWrite(MemWrite),
    .ALU_SRC(ALU_SRC), .RegWrite(RegWrite), .SysCALL(SysCALL), .SignedExt(SignedExt), .RegDst(RegDst),
    .BEQ(Beq), .BNE(Bne), .JR(JR), .JMP(JMP), .JAL(JAL));
  Comparator #(.width(6), .mode("unsigned")) comparator_5 (
    .a(Func), .b(6'b000111), .eq(comparator_5_eq));  // open: gt, lt
  and and_1 (SRAV, comparator_5_eq, comparator_1_eq);

  // Other names for the same wires on the sheet: OP_CODE[5:0] = OP

  // Notes on the sheet:
  //   运算器控制器，根据指令生成运算器功能选择信号
  //   控制信号生成，产生数据通路需要的其他控制信号
endmodule

// 运算器控制器
module \运算控制器  (
  input  OP0,
  input  OP1,
  input  OP2,
  input  OP3,
  input  OP4,
  input  OP5,
  input  F0,
  input  F1,
  input  F2,
  input  F3,
  input  F4,
  input  F5,
  output S0,
  output S1,
  output S2,
  output S3
);

  wire and_1_out, and_2_out, and_3_out, and_4_out, and_5_out, and_6_out, and_7_out, and_8_out, and_9_out,
       and_10_out, and_11_out, and_12_out, and_13_out, and_14_out, and_15_out, and_16_out, and_17_out,
       and_18_out, and_19_out, and_20_out, and_21_out, and_22_out, and_23_out, and_24_out, and_25_out,
       and_26_out, and_27_out, and_28_out, and_29_out, and_30_out, and_31_out, and_32_out, and_33_out,
       and_34_out, and_35_out, and_36_out, and_37_out, and_38_out, and_39_out, and_40_out, and_41_out,
       and_42_out, not_1_out, not_2_out, not_3_out, not_4_out, not_5_out, not_6_out, not_7_out, not_8_out,
       not_9_out, not_10_out, not_11_out, not_12_out, not_13_out, not_14_out, not_15_out, not_16_out,
       not_17_out, not_18_out, not_19_out, not_20_out, not_21_out, not_22_out, not_23_out, not_24_out,
       not_25_out, not_26_out, not_27_out, not_28_out, not_29_out, not_30_out, not_31_out, not_32_out,
       not_33_out, not_34_out, not_35_out, not_36_out, not_37_out, not_38_out, not_39_out, not_40_out,
       not_41_out, not_42_out, not_43_out, not_44_out, not_45_out, not_46_out, not_47_out, not_48_out,
       not_49_out, not_50_out, not_51_out, not_52_out, not_53_out, not_54_out, not_55_out, not_56_out,
       not_57_out, not_58_out, not_59_out, not_60_out, not_61_out, not_62_out, not_63_out, not_64_out,
       not_65_out, not_66_out, not_67_out, not_68_out, not_69_out, not_70_out, not_71_out, not_72_out,
       not_73_out, not_74_out, not_75_out, not_76_out, not_77_out, not_78_out, not_79_out, not_80_out,
       not_81_out, not_82_out, not_83_out, not_84_out, not_85_out, not_86_out, not_87_out, not_88_out,
       not_89_out, not_90_out, not_91_out, not_92_out, not_93_out, not_94_out, not_95_out, not_96_out,
       not_97_out, not_98_out, not_99_out, not_100_out, not_101_out, not_102_out, not_103_out, not_104_out,
       not_105_out, not_106_out, not_107_out, not_108_out, not_109_out, not_110_out, not_111_out,
       not_112_out, not_113_out, not_114_out, not_115_out, not_116_out, not_117_out, not_118_out,
       not_119_out, not_120_out, not_121_out, not_122_out, not_123_out, not_124_out, not_125_out,
       not_126_out, not_127_out, not_128_out, not_129_out, not_130_out, not_131_out, not_132_out,
       not_133_out, not_134_out, not_135_out, not_136_out, not_137_out, not_138_out, not_139_out,
       not_140_out, not_141_out, not_142_out, not_143_out, not_144_out, not_145_out, not_146_out,
       not_147_out, not_148_out, not_149_out, not_150_out, not_151_out, not_152_out, not_153_out,
       not_154_out, not_155_out, not_156_out, not_157_out, not_158_out, not_159_out, not_160_out,
       not_161_out, not_162_out, not_163_out, not_164_out, not_165_out, not_166_out, not_167_out,
       not_168_out, not_169_out, not_170_out, not_171_out, not_172_out, not_173_out, not_174_out,
       not_175_out, not_176_out, not_177_out, not_178_out, not_179_out, not_180_out, not_181_out,
       not_182_out, not_183_out, not_184_out, not_185_out, not_186_out, not_187_out, not_188_out,
       not_189_out, not_190_out, not_191_out, not_192_out, not_193_out, not_194_out, not_195_out,
       not_196_out, not_197_out, not_198_out, not_199_out, not_200_out, not_201_out, not_202_out,
       not_203_out, not_204_out, not_205_out, not_206_out, not_207_out, not_208_out, not_209_out,
       not_210_out, not_211_out, not_212_out, not_213_out, not_214_out, not_215_out, not_216_out,
       not_217_out, not_218_out, not_219_out, not_220_out, not_221_out, not_222_out, not_223_out,
       not_224_out, not_225_out, not_226_out, not_227_out, not_228_out, not_229_out, not_230_out,
       not_231_out, not_232_out, not_233_out, not_234_out, not_235_out, not_236_out, not_237_out,
       not_238_out, not_239_out, not_240_out, not_241_out, not_242_out, not_243_out, not_244_out,
       not_245_out, not_246_out, not_247_out, not_248_out, not_249_out, not_250_out, not_251_out,
       not_252_out, not_253_out, not_254_out, not_255_out, not_256_out, not_257_out, not_258_out,
       not_259_out, not_260_out, not_261_out, not_262_out, not_263_out, not_264_out, not_265_out,
       not_266_out, not_267_out, not_268_out, not_269_out, not_270_out, not_271_out, not_272_out;

  not not_1 (not_1_out, OP5);
  not not_2 (not_2_out, OP4);
  not not_3 (not_3_out, OP3);
  not not_4 (not_4_out, OP2);
  not not_5 (not_5_out, OP1);
  not not_6 (not_6_out, OP0);
  not not_7 (not_7_out, F5);
  not not_8 (not_8_out, F4);
  not not_9 (not_9_out, F3);
  not not_10 (not_10_out, F2);
  not not_11 (not_11_out, OP5);
  not not_12 (not_12_out, OP4);
  not not_13 (not_13_out, OP3);
  not not_14 (not_14_out, OP2);
  not not_15 (not_15_out, OP1);
  not not_16 (not_16_out, OP0);
  not not_17 (not_17_out, F4);
  not not_18 (not_18_out, F3);
  not not_19 (not_19_out, F2);
  not not_20 (not_20_out, F1);
  not not_21 (not_21_out, F0);
  not not_22 (not_22_out, OP5);
  not not_23 (not_23_out, OP4);
  not not_24 (not_24_out, OP3);
  not not_25 (not_25_out, OP2);
  not not_26 (not_26_out, OP1);
  not not_27 (not_27_out, OP0);
  not not_28 (not_28_out, F4);
  not not_29 (not_29_out, F3);
  not not_30 (not_30_out, F2);
  not not_31 (not_31_out, F1);
  not not_32 (not_32_out, OP5);
  not not_33 (not_33_out, OP4);
  not not_34 (not_34_out, OP3);
  not not_35 (not_35_out, OP2);
  not not_36 (not_36_out, OP1);
  not not_37 (not_37_out, OP0);
  not not_38 (not_38_out, F4);
  not not_39 (not_39_out, F3);
  not not_40 (not_40_out, F1);
  not not_41 (not_41_out, F0);
  not not_42 (not_42_out, OP5);
  not not_43 (not_43_out, OP4);
  not not_44 (not_44_out, OP3);
  not not_45 (not_45_out, OP2);
  not not_46 (not_46_out, OP1);
  not not_47 (not_47_out, OP0);
  not not_48 (not_48_out, F4);
  not not_49 (not_49_out, F2);
  not not_50 (not_50_out, F0);
  not not_51 (not_51_out, OP5);
  not not_52 (not_52_out, OP4);
  not not_53 (not_53_out, OP2);
  not not_54 (not_54_out, OP1);
  not not_55 (not_55_out, OP0);
  not not_56 (not_56_out, OP5);
  not not_57 (not_57_out, OP4);
  not not_58 (not_58_out, OP1);
  not not_59 (not_59_out, OP0);
  not not_60 (not_60_out, OP5);
  not not_61 (not_61_out, OP4);
  not not_62 (not_62_out, OP2);
  not not_63 (not_63_out, OP1);
  not not_64 (not_64_out, OP5);
  not not_65 (not_65_out, OP4);
  not not_66 (not_66_out, OP2);
  not not_67 (not_67_out, OP0);
  not not_68 (not_68_out, OP4);
  not not_69 (not_69_out, OP3);
  not not_70 (not_70_out, OP2);
  not not_71 (not_71_out, OP4);
  not not_72 (not_72_out, OP2);
  not not_73 (not_73_out, OP5);
  not not_74 (not_74_out, OP4);
  not not_75 (not_75_out, OP3);
  not not_76 (not_76_out, OP2);
  not not_77 (not_77_out, OP1);
  not not_78 (not_78_out, OP0);
  not not_79 (not_79_out, F5);
  not not_80 (not_80_out, F4);
  not not_81 (not_81_out, F3);
  not not_82 (not_82_out, OP4);
  not not_83 (not_83_out, OP3);
  not not_84 (not_84_out, OP1);
  not not_85 (not_85_out, OP5);
  not not_86 (not_86_out, OP4);
  not not_87 (not_87_out, OP3);
  not not_88 (not_88_out, OP2);
  not not_89 (not_89_out, OP1);
  not not_90 (not_90_out, OP5);
  not not_91 (not_91_out, OP4);
  not not_92 (not_92_out, OP3);
  not not_93 (not_93_out, OP2);
  not not_94 (not_94_out, OP1);
  not not_95 (not_95_out, OP0);
  not not_96 (not_96_out, F5);
  not not_97 (not_97_out, F4);
  not not_98 (not_98_out, F3);
  not not_99 (not_99_out, F2);
  not not_100 (not_100_out, F0);
  not not_101 (not_101_out, OP5);
  not not_102 (not_102_out, OP4);
  not not_103 (not_103_out, OP3);
  not not_104 (not_104_out, OP2);
  not not_105 (not_105_out, OP1);
  not not_106 (not_106_out, OP0);
  not not_107 (not_107_out, F4);
  not not_108 (not_108_out, F3);
  not not_109 (not_109_out, F2);
  not not_110 (not_110_out, F0);
  not not_111 (not_111_out, OP5);
  not not_112 (not_112_out, OP4);
  not not_113 (not_113_out, OP3);
  not not_114 (not_114_out, OP2);
  not not_115 (not_115_out, OP1);
  not not_116 (not_116_out, OP0);
  not not_117 (not_117_out, F4);
  not not_118 (not_118_out, F3);
  not not_119 (not_119_out, F1);
  not not_120 (not_120_out, F0);
  not not_121 (not_121_out, OP5);
  not not_122 (not_122_out, OP4);
  not not_123 (not_123_out, OP3);
  not not_124 (not_124_out, OP2);
  not not_125 (not_125_out, OP1);
  not not_126 (not_126_out, OP0);
  not not_127 (not_127_out, F4);
  not not_128 (not_128_out, F3);
  not not_129 (not_129_out, OP5);
  not not_130 (not_130_out, OP4);
  not not_131 (not_131_out, OP3);
  not not_132 (not_132_out, OP2);
  not not_133 (not_133_out, OP1);
  not not_134 (not_134_out, OP0);
  not not_135 (not_135_out, F4);
  not not_136 (not_136_out, F2);
  not not_137 (not_137_out, F0);
  not not_138 (not_138_out, OP5);
  not not_139 (not_139_out, OP4);
  not not_140 (not_140_out, OP1);
  not not_141 (not_141_out, OP0);
  not not_142 (not_142_out, OP5);
  not not_143 (not_143_out, OP4);
  not not_144 (not_144_out, OP2);
  not not_145 (not_145_out, OP0);
  not not_146 (not_146_out, OP5);
  not not_147 (not_147_out, OP4);
  not not_148 (not_148_out, OP3);
  not not_149 (not_149_out, OP2);
  not not_150 (not_150_out, OP1);
  not not_151 (not_151_out, OP5);
  not not_152 (not_152_out, OP4);
  not not_153 (not_153_out, OP3);
  not not_154 (not_154_out, OP2);
  not not_155 (not_155_out, OP1);
  not not_156 (not_156_out, OP0);
  not not_157 (not_157_out, F4);
  not not_158 (not_158_out, F3);
  not not_159 (not_159_out, F2);
  not not_160 (not_160_out, F1);
  not not_161 (not_161_out, F0);
  not not_162 (not_162_out, OP5);
  not not_163 (not_163_out, OP4);
  not not_164 (not_164_out, OP3);
  not not_165 (not_165_out, OP2);
  not not_166 (not_166_out, OP1);
  not not_167 (not_167_out, OP0);
  not not_168 (not_168_out, F4);
  not not_169 (not_169_out, F3);
  not not_170 (not_170_out, F2);
  not not_171 (not_171_out, F1);
  not not_172 (not_172_out, OP5);
  not not_173 (not_173_out, OP4);
  not not_174 (not_174_out, OP3);
  not not_175 (not_175_out, OP2);
  not not_176 (not_176_out, OP1);
  not not_177 (not_177_out, OP0);
  not not_178 (not_178_out, F4);
  not not_179 (not_179_out, F3);
  not not_180 (not_180_out, F2);
  not not_181 (not_181_out, F0);
  not not_182 (not_182_out, OP5);
  not not_183 (not_183_out, OP4);
  not not_184 (not_184_out, OP3);
  not not_185 (not_185_out, OP2);
  not not_186 (not_186_out, OP1);
  not not_187 (not_187_out, OP0);
  not not_188 (not_188_out, F4);
  not not_189 (not_189_out, F3);
  not not_190 (not_190_out, F1);
  not not_191 (not_191_out, F0);
  not not_192 (not_192_out, OP5);
  not not_193 (not_193_out, OP4);
  not not_194 (not_194_out, OP3);
  not not_195 (not_195_out, OP2);
  not not_196 (not_196_out, OP1);
  not not_197 (not_197_out, OP0);
  not not_198 (not_198_out, F4);
  not not_199 (not_199_out, F2);
  not not_200 (not_200_out, OP5);
  not not_201 (not_201_out, OP4);
  not not_202 (not_202_out, OP2);
  not not_203 (not_203_out, OP1);
  not not_204 (not_204_out, OP0);
  not not_205 (not_205_out, OP5);
  not not_206 (not_206_out, OP4);
  not not_207 (not_207_out, OP1);
  not not_208 (not_208_out, OP0);
  not not_209 (not_209_out, OP5);
  not not_210 (not_210_out, OP4);
  not not_211 (not_211_out, OP2);
  not not_212 (not_212_out, OP1);
  not not_213 (not_213_out, OP4);
  not not_214 (not_214_out, OP3);
  not not_215 (not_215_out, OP2);
  not not_216 (not_216_out, OP4);
  not not_217 (not_217_out, OP2);
  not not_218 (not_218_out, OP5);
  not not_219 (not_219_out, OP4);
  not not_220 (not_220_out, OP2);
  not not_221 (not_221_out, OP4);
  not not_222 (not_222_out, OP3);
  not not_223 (not_223_out, OP1);
  not not_224 (not_224_out, OP5);
  not not_225 (not_225_out, OP4);
  not not_226 (not_226_out, OP3);
  not not_227 (not_227_out, OP2);
  not not_228 (not_228_out, OP1);
  not not_229 (not_229_out, OP0);
  not not_230 (not_230_out, F4);
  not not_231 (not_231_out, F3);
  not not_232 (not_232_out, F1);
  not not_233 (not_233_out, OP5);
  not not_234 (not_234_out, OP4);
  not not_235 (not_235_out, OP3);
  not not_236 (not_236_out, OP2);
  not not_237 (not_237_out, OP1);
  not not_238 (not_238_out, OP0);
  not not_239 (not_239_out, F4);
  not not_240 (not_240_out, F3);
  not not_241 (not_241_out, OP5);
  not not_242 (not_242_out, OP4);
  not not_243 (not_243_out, OP3);
  not not_244 (not_244_out, OP2);
  not not_245 (not_245_out, OP1);
  not not_246 (not_246_out, OP0);
  not not_247 (not_247_out, F4);
  not not_248 (not_248_out, F2);
  not not_249 (not_249_out, F0);
  not not_250 (not_250_out, OP5);
  not not_251 (not_251_out, OP4);
  not not_252 (not_252_out, OP3);
  not not_253 (not_253_out, OP2);
  not not_254 (not_254_out, OP1);
  not not_255 (not_255_out, OP0);
  not not_256 (not_256_out, F4);
  not not_257 (not_257_out, F2);
  not not_258 (not_258_out, OP5);
  not not_259 (not_259_out, OP4);
  not not_260 (not_260_out, OP2);
  not not_261 (not_261_out, OP0);
  not not_262 (not_262_out, OP5);
  not not_263 (not_263_out, OP4);
  not not_264 (not_264_out, OP1);
  not not_265 (not_265_out, OP5);
  not not_266 (not_266_out, OP4);
  not not_267 (not_267_out, OP2);
  not not_268 (not_268_out, OP5);
  not not_269 (not_269_out, OP4);
  not not_270 (not_270_out, OP3);
  not not_271 (not_271_out, OP2);
  not not_272 (not_272_out, OP1);
  and and_1 (and_1_out, not_1_out, not_2_out, not_3_out, not_4_out, not_5_out, not_6_out, not_7_out, not_8_out, not_9_out, not_10_out, F1, F0);
  and and_2 (and_2_out, not_11_out, not_12_out, not_13_out, not_14_out, not_15_out, not_16_out, F5, not_17_out, not_18_out, not_19_out, not_20_out, not_21_out);
  and and_3 (and_3_out, not_22_out, not_23_out, not_24_out, not_25_out, not_26_out, not_27_out, F5, not_28_out, not_29_out, not_30_out, not_31_out, F0);
  and and_4 (and_4_out, not_32_out, not_33_out, not_34_out, not_35_out, not_36_out, not_37_out, F5, not_38_out, not_39_out, F2, not_40_out, not_41_out);
  and and_5 (and_5_out, not_42_out, not_43_out, not_44_out, not_45_out, not_46_out, not_47_out, F5, not_48_out, F3, not_49_out, F1, not_50_out);
  and and_6 (and_6_out, not_51_out, not_52_out, OP3, not_53_out, not_54_out, not_55_out);
  and and_7 (and_7_out, not_56_out, not_57_out, OP3, OP2, not_58_out, not_59_out);
  and and_8 (and_8_out, not_60_out, not_61_out, OP3, not_62_out, not_63_out, OP0);
  and and_9 (and_9_out, not_64_out, not_65_out, OP3, not_66_out, OP1, not_67_out);
  and and_10 (and_10_out, OP5, not_68_out, not_69_out, not_70_out, OP1, OP0);
  and and_11 (and_11_out, OP5, not_71_out, OP3, not_72_out, OP1, OP0);
  and and_12 (and_12_out, not_73_out, not_74_out, not_75_out, not_76_out, not_77_out, not_78_out, not_79_out, not_80_out, not_81_out, F2, F1, F0);
  and and_13 (and_13_out, OP5, not_82_out, not_83_out, OP2, not_84_out, OP0);
  and and_14 (and_14_out, not_85_out, not_86_out, not_87_out, not_88_out, not_89_out, OP0);
  and and_15 (and_15_out, not_90_out, not_91_out, not_92_out, not_93_out, not_94_out, not_95_out, not_96_out, not_97_out, not_98_out, not_99_out, F1, not_100_out);
  and and_16 (and_16_out, not_101_out, not_102_out, not_103_out, not_104_out, not_105_out, not_106_out, F5, not_107_out, not_108_out, not_109_out, F1, not_110_out);
  and and_17 (and_17_out, not_111_out, not_112_out, not_113_out, not_114_out, not_115_out, not_116_out, F5, not_117_out, not_118_out, F2, not_119_out, not_120_out);
  and and_18 (and_18_out, not_121_out, not_122_out, not_123_out, not_124_out, not_125_out, not_126_out, F5, not_127_out, not_128_out, F2, F1, F0);
  and and_19 (and_19_out, not_129_out, not_130_out, not_131_out, not_132_out, not_133_out, not_134_out, F5, not_135_out, F3, not_136_out, F1, not_137_out);
  and and_20 (and_20_out, not_138_out, not_139_out, OP3, OP2, not_140_out, not_141_out);
  and and_21 (and_21_out, not_142_out, not_143_out, OP3, not_144_out, OP1, not_145_out);
  and and_22 (and_22_out, not_146_out, not_147_out, not_148_out, not_149_out, not_150_out, OP0);
  and and_23 (and_23_out, not_151_out, not_152_out, not_153_out, not_154_out, not_155_out, not_156_out, F5, not_157_out, not_158_out, not_159_out, not_160_out, not_161_out);
  and and_24 (and_24_out, not_162_out, not_163_out, not_164_out, not_165_out, not_166_out, not_167_out, F5, not_168_out, not_169_out, not_170_out, not_171_out, F0);
  and and_25 (and_25_out, not_172_out, not_173_out, not_174_out, not_175_out, not_176_out, not_177_out, F5, not_178_out, not_179_out, not_180_out, F1, not_181_out);
  and and_26 (and_26_out, not_182_out, not_183_out, not_184_out, not_185_out, not_186_out, not_187_out, F5, not_188_out, not_189_out, F2, not_190_out, not_191_out);
  and and_27 (and_27_out, not_192_out, not_193_out, not_194_out, not_195_out, not_196_out, not_197_out, F5, not_198_out, F3, not_199_out, F1, F0);
  and and_28 (and_28_out, not_200_out, not_201_out, OP3, not_202_out, not_203_out, not_204_out);
  and and_29 (and_29_out, not_205_out, not_206_out, OP3, OP2, not_207_out, not_208_out);
  and and_30 (and_30_out, not_209_out, not_210_out, OP3, not_211_out, not_212_out, OP0);
  and and_31 (and_31_out, OP5, not_213_out, not_214_out, not_215_out, OP1, OP0);
  and and_32 (and_32_out, OP5, not_216_out, OP3, not_217_out, OP1, OP0);
  and and_33 (and_33_out, not_218_out, not_219_out, OP3, not_220_out, OP1, OP0);
  and and_34 (and_34_out, OP5, not_221_out, not_222_out, OP2, not_223_out, OP0);
  and and_35 (and_35_out, not_224_out, not_225_out, not_226_out, not_227_out, not_228_out, not_229_out, F5, not_230_out, not_231_out, F2, not_232_out, F0);
  and and_36 (and_36_out, not_233_out, not_234_out, not_235_out, not_236_out, not_237_out, not_238_out, F5, not_239_out, not_240_out, F2, F1, F0);
  and and_37 (and_37_out, not_241_out, not_242_out, not_243_out, not_244_out, not_245_out, not_246_out, F5, not_247_out, F3, not_248_out, F1, not_249_out);
  and and_38 (and_38_out, not_250_out, not_251_out, not_252_out, not_253_out, not_254_out, not_255_out, F5, not_256_out, F3, not_257_out, F1, F0);
  and and_39 (and_39_out, not_258_out, not_259_out, OP3, not_260_out, OP1, not_261_out);
  and and_40 (and_40_out, not_262_out, not_263_out, OP3, OP2, not_264_out, OP0);
  and and_41 (and_41_out, not_265_out, not_266_out, OP3, not_267_out, OP1, OP0);
  and and_42 (and_42_out, not_268_out, not_269_out, not_270_out, not_271_out, not_272_out, OP0);
  or or_1 (S1, and_15_out, and_16_out, and_17_out, and_18_out, and_19_out, and_20_out, and_21_out, and_22_out);
  or or_2 (S3, and_35_out, and_36_out, and_37_out, and_38_out, and_39_out, and_40_out, and_41_out, and_42_out);
  or or_3 (S0, and_1_out, and_2_out, and_3_out, and_4_out, and_5_out, and_6_out, and_7_out, and_8_out, and_9_out, and_10_out, and_11_out, and_12_out, and_13_out, and_14_out);
  or or_4 (S2, and_23_out, and_24_out, and_25_out, and_26_out, and_27_out, and_28_out, and_29_out, and_30_out, and_31_out, and_32_out, and_33_out, and_34_out);
endmodule

// 控制信号生成
module \控制信号生成  (
  input  OP0,
  input  OP1,
  input  OP2,
  input  OP3,
  input  OP4,
  input  OP5,
  input  F0,
  input  F1,
  input  F2,
  input  F3,
  input  F4,
  input  F5,
  output MemToReg,
  output MemWrite,
  output ALU_SRC,
  output RegWrite,
  output SysCALL,
  output SignedExt,
  output RegDst,
  output BEQ,
  output BNE,
  output JR,
  output JMP,
  output JAL
);

  wire and_1_out, and_2_out, and_4_out, and_5_out, and_6_out, and_7_out, and_8_out, and_9_out, and_10_out,
       and_11_out, and_12_out, and_13_out, and_14_out, and_15_out, and_16_out, and_17_out, and_18_out,
       and_19_out, and_20_out, and_21_out, and_22_out, and_23_out, and_24_out, and_25_out, and_26_out,
       and_27_out, and_28_out, and_29_out, and_30_out, and_31_out, and_32_out, and_33_out, and_34_out,
       and_36_out, and_37_out, and_38_out, and_39_out, and_40_out, and_41_out, and_42_out, and_43_out,
       and_44_out, and_45_out, and_46_out, and_47_out, and_48_out, and_49_out, and_50_out, and_51_out,
       and_52_out, and_53_out, and_54_out, and_55_out, and_56_out, and_57_out, and_58_out, and_59_out,
       and_63_out, and_64_out, and_65_out, not_1_out, not_2_out, not_3_out, not_4_out, not_5_out, not_6_out,
       not_7_out, not_8_out, not_9_out, not_10_out, not_11_out, not_12_out, not_13_out, not_14_out,
       not_15_out, not_16_out, not_17_out, not_18_out, not_19_out, not_20_out, not_21_out, not_22_out,
       not_23_out, not_24_out, not_25_out, not_26_out, not_27_out, not_28_out, not_29_out, not_30_out,
       not_31_out, not_32_out, not_33_out, not_34_out, not_35_out, not_36_out, not_37_out, not_38_out,
       not_39_out, not_40_out, not_41_out, not_42_out, not_43_out, not_44_out, not_45_out, not_46_out,
       not_47_out, not_48_out, not_49_out, not_50_out, not_51_out, not_52_out, not_53_out, not_54_out,
       not_55_out, not_56_out, not_57_out, not_58_out, not_59_out, not_60_out, not_61_out, not_62_out,
       not_63_out, not_64_out, not_65_out, not_66_out, not_67_out, not_68_out, not_69_out, not_70_out,
       not_71_out, not_72_out, not_73_out, not_74_out, not_75_out, not_76_out, not_77_out, not_78_out,
       not_79_out, not_80_out, not_81_out, not_82_out, not_83_out, not_84_out, not_85_out, not_86_out,
       not_87_out, not_88_out, not_89_out, not_90_out, not_91_out, not_92_out, not_93_out, not_94_out,
       not_95_out, not_96_out, not_97_out, not_98_out, not_99_out, not_100_out, not_101_out, not_102_out,
       not_103_out, not_104_out, not_105_out, not_106_out, not_107_out, not_108_out, not_109_out,
       not_110_out, not_111_out, not_112_out, not_113_out, not_114_out, not_115_out, not_116_out,
       not_117_out, not_118_out, not_119_out, not_120_out, not_121_out, not_122_out, not_123_out,
       not_124_out, not_125_out, not_126_out, not_127_out, not_128_out, not_129_out, not_130_out,
       not_131_out, not_132_out, not_133_out, not_134_out, not_135_out, not_136_out, not_137_out,
       not_138_out, not_139_out, not_140_out, not_141_out, not_142_out, not_143_out, not_144_out,
       not_145_out, not_146_out, not_147_out, not_148_out, not_149_out, not_150_out, not_151_out,
       not_152_out, not_153_out, not_154_out, not_155_out, not_156_out, not_157_out, not_158_out,
       not_159_out, not_160_out, not_161_out, not_162_out, not_163_out, not_164_out, not_165_out,
       not_166_out, not_167_out, not_168_out, not_169_out, not_170_out, not_171_out, not_172_out,
       not_173_out, not_174_out, not_175_out, not_176_out, not_177_out, not_178_out, not_179_out,
       not_180_out, not_181_out, not_182_out, not_183_out, not_184_out, not_185_out, not_186_out,
       not_187_out, not_188_out, not_189_out, not_190_out, not_191_out, not_192_out, not_193_out,
       not_194_out, not_195_out, not_196_out, not_197_out, not_198_out, not_199_out, not_200_out,
       not_201_out, not_202_out, not_203_out, not_204_out, not_205_out, not_206_out, not_207_out,
       not_208_out, not_209_out, not_210_out, not_211_out, not_212_out, not_213_out, not_214_out,
       not_215_out, not_216_out, not_217_out, not_218_out, not_219_out, not_220_out, not_221_out,
       not_222_out, not_223_out, not_224_out, not_225_out, not_226_out, not_227_out, not_228_out,
       not_229_out, not_230_out, not_231_out, not_232_out, not_233_out, not_234_out, not_235_out,
       not_236_out, not_237_out, not_238_out, not_239_out, not_240_out, not_241_out, not_242_out,
       not_243_out, not_244_out, not_245_out, not_246_out, not_247_out, not_248_out, not_249_out,
       not_250_out, not_251_out, not_252_out, not_253_out, not_254_out, not_255_out, not_256_out,
       not_257_out, not_258_out, not_259_out, not_260_out, not_261_out, not_262_out, not_263_out,
       not_264_out, not_265_out, not_266_out, not_267_out, not_268_out, not_269_out, not_270_out,
       not_271_out, not_272_out, not_273_out, not_274_out, not_275_out, not_276_out, not_277_out,
       not_278_out, not_279_out, not_280_out, not_281_out, not_282_out, not_283_out, not_284_out,
       not_285_out, not_286_out, not_287_out, not_288_out, not_289_out, not_290_out, not_291_out,
       not_292_out, not_293_out, not_294_out, not_295_out, not_296_out, not_297_out, not_298_out,
       not_299_out, not_300_out, not_301_out, not_302_out, not_303_out, not_304_out, not_305_out,
       not_306_out, not_307_out, not_308_out, not_309_out, not_310_out, not_311_out, not_312_out,
       not_313_out, not_314_out, not_315_out, not_316_out, not_317_out, not_318_out, not_319_out,
       not_320_out, not_321_out, not_322_out, not_323_out, not_324_out, not_325_out, not_326_out,
       not_327_out, not_328_out, not_329_out, not_330_out, not_331_out, not_332_out, not_333_out,
       not_334_out, not_335_out, not_336_out, not_337_out, not_338_out, not_339_out, not_340_out,
       not_341_out, not_342_out, not_343_out, not_344_out, not_345_out, not_346_out, not_347_out,
       not_348_out, not_349_out, not_350_out, not_351_out, not_352_out, not_353_out, not_354_out,
       not_355_out, not_356_out, not_357_out, not_358_out, not_359_out, not_360_out, not_361_out,
       not_362_out, not_363_out, not_364_out, not_365_out, not_366_out, not_367_out, not_368_out,
       not_369_out, not_370_out, not_371_out, not_372_out, not_373_out, not_374_out, not_375_out,
       not_376_out, not_377_out, not_378_out, not_379_out, not_380_out, not_381_out, not_382_out,
       not_383_out, not_384_out, not_385_out, not_386_out, not_387_out, not_388_out, not_389_out,
       not_390_out, not_391_out, not_392_out, not_393_out, not_394_out, not_395_out, not_396_out,
       not_397_out, not_398_out, not_399_out, not_400_out, not_401_out, not_402_out, not_403_out,
       not_404_out, not_405_out, not_406_out, not_407_out, not_408_out, not_409_out, not_410_out,
       not_411_out, not_412_out, not_413_out, not_414_out, not_415_out, not_416_out, not_417_out,
       not_418_out, not_419_out, not_420_out, not_421_out, not_422_out, not_423_out, not_424_out;

  not not_1 (not_1_out, OP4);
  not not_2 (not_2_out, OP3);
  not not_3 (not_3_out, OP2);
  not not_4 (not_4_out, OP4);
  not not_5 (not_5_out, OP3);
  not not_6 (not_6_out, OP1);
  not not_7 (not_7_out, OP4);
  not not_8 (not_8_out, OP2);
  not not_9 (not_9_out, OP5);
  not not_10 (not_10_out, OP4);
  not not_11 (not_11_out, OP2);
  not not_12 (not_12_out, OP1);
  not not_13 (not_13_out, OP0);
  not not_14 (not_14_out, OP5);
  not not_15 (not_15_out, OP4);
  not not_16 (not_16_out, OP1);
  not not_17 (not_17_out, OP0);
  not not_18 (not_18_out, OP5);
  not not_19 (not_19_out, OP4);
  not not_20 (not_20_out, OP2);
  not not_21 (not_21_out, OP1);
  not not_22 (not_22_out, OP5);
  not not_23 (not_23_out, OP4);
  not not_24 (not_24_out, OP2);
  not not_25 (not_25_out, OP0);
  not not_26 (not_26_out, OP5);
  not not_27 (not_27_out, OP4);
  not not_28 (not_28_out, OP1);
  not not_29 (not_29_out, OP4);
  not not_30 (not_30_out, OP3);
  not not_31 (not_31_out, OP2);
  not not_32 (not_32_out, OP4);
  not not_33 (not_33_out, OP2);
  not not_34 (not_34_out, OP5);
  not not_35 (not_35_out, OP4);
  not not_36 (not_36_out, OP2);
  not not_37 (not_37_out, OP4);
  not not_38 (not_38_out, OP3);
  not not_39 (not_39_out, OP1);
  not not_40 (not_40_out, OP5);
  not not_41 (not_41_out, OP4);
  not not_42 (not_42_out, OP3);
  not not_43 (not_43_out, OP2);
  not not_44 (not_44_out, OP1);
  not not_45 (not_45_out, OP5);
  not not_46 (not_46_out, OP4);
  not not_47 (not_47_out, OP3);
  not not_48 (not_48_out, OP2);
  not not_49 (not_49_out, OP1);
  not not_50 (not_50_out, OP0);
  not not_51 (not_51_out, F5);
  not not_52 (not_52_out, F4);
  not not_53 (not_53_out, F3);
  not not_54 (not_54_out, F2);
  not not_55 (not_55_out, F1);
  not not_56 (not_56_out, F0);
  not not_57 (not_57_out, OP5);
  not not_58 (not_58_out, OP4);
  not not_59 (not_59_out, OP3);
  not not_60 (not_60_out, OP2);
  not not_61 (not_61_out, OP1);
  not not_62 (not_62_out, OP0);
  not not_63 (not_63_out, F5);
  not not_64 (not_64_out, F4);
  not not_65 (not_65_out, F3);
  not not_66 (not_66_out, F2);
  not not_67 (not_67_out, OP5);
  not not_68 (not_68_out, OP4);
  not not_69 (not_69_out, OP3);
  not not_70 (not_70_out, OP2);
  not not_71 (not_71_out, OP1);
  not not_72 (not_72_out, OP0);
  not not_73 (not_73_out, F5);
  not not_74 (not_74_out, F4);
  not not_75 (not_75_out, F3);
  not not_76 (not_76_out, F2);
  not not_77 (not_77_out, F0);
  not not_78 (not_78_out, OP5);
  not not_79 (not_79_out, OP4);
  not not_80 (not_80_out, OP3);
  not not_81 (not_81_out, OP2);
  not not_82 (not_82_out, OP1);
  not not_83 (not_83_out, OP0);
  not not_84 (not_84_out, F4);
  not not_85 (not_85_out, F3);
  not not_86 (not_86_out, F2);
  not not_87 (not_87_out, F1);
  not not_88 (not_88_out, F0);
  not not_89 (not_89_out, OP5);
  not not_90 (not_90_out, OP4);
  not not_91 (not_91_out, OP3);
  not not_92 (not_92_out, OP2);
  not not_93 (not_93_out, OP1);
  not not_94 (not_94_out, OP0);
  not not_95 (not_95_out, F4);
  not not_96 (not_96_out, F3);
  not not_97 (not_97_out, F2);
  not not_98 (not_98_out, F1);
  not not_99 (not_99_out, OP5);
  not not_100 (not_100_out, OP4);
  not not_101 (not_101_out, OP3);
  not not_102 (not_102_out, OP2);
  not not_103 (not_103_out, OP1);
  not not_104 (not_104_out, OP0);
  not not_105 (not_105_out, F4);
  not not_106 (not_106_out, F3);
  not not_107 (not_107_out, F2);
  not not_108 (not_108_out, F0);
  not not_109 (not_109_out, OP5);
  not not_110 (not_110_out, OP4);
  not not_111 (not_111_out, OP3);
  not not_112 (not_112_out, OP2);
  not not_113 (not_113_out, OP1);
  not not_114 (not_114_out, OP0);
  not not_115 (not_115_out, F4);
  not not_116 (not_116_out, F3);
  not not_117 (not_117_out, F1);
  not not_118 (not_118_out, F0);
  not not_119 (not_119_out, OP5);
  not not_120 (not_120_out, OP4);
  not not_121 (not_121_out, OP3);
  not not_122 (not_122_out, OP2);
  not not_123 (not_123_out, OP1);
  not not_124 (not_124_out, OP0);
  not not_125 (not_125_out, F4);
  not not_126 (not_126_out, F3);
  not not_127 (not_127_out, F1);
  not not_128 (not_128_out, OP5);
  not not_129 (not_129_out, OP4);
  not not_130 (not_130_out, OP3);
  not not_131 (not_131_out, OP2);
  not not_132 (not_132_out, OP1);
  not not_133 (not_133_out, OP0);
  not not_134 (not_134_out, F4);
  not not_135 (not_135_out, F3);
  not not_136 (not_136_out, OP5);
  not not_137 (not_137_out, OP4);
  not not_138 (not_138_out, OP3);
  not not_139 (not_139_out, OP2);
  not not_140 (not_140_out, OP1);
  not not_141 (not_141_out, OP0);
  not not_142 (not_142_out, F4);
  not not_143 (not_143_out, F2);
  not not_144 (not_144_out, F0);
  not not_145 (not_145_out, OP5);
  not not_146 (not_146_out, OP4);
  not not_147 (not_147_out, OP3);
  not not_148 (not_148_out, OP2);
  not not_149 (not_149_out, OP1);
  not not_150 (not_150_out, OP0);
  not not_151 (not_151_out, F4);
  not not_152 (not_152_out, F2);
  not not_153 (not_153_out, OP5);
  not not_154 (not_154_out, OP4);
  not not_155 (not_155_out, OP3);
  not not_156 (not_156_out, OP2);
  not not_157 (not_157_out, OP5);
  not not_158 (not_158_out, OP4);
  not not_159 (not_159_out, OP2);
  not not_160 (not_160_out, OP1);
  not not_161 (not_161_out, OP0);
  not not_162 (not_162_out, OP5);
  not not_163 (not_163_out, OP4);
  not not_164 (not_164_out, OP1);
  not not_165 (not_165_out, OP0);
  not not_166 (not_166_out, OP5);
  not not_167 (not_167_out, OP4);
  not not_168 (not_168_out, OP2);
  not not_169 (not_169_out, OP1);
  not not_170 (not_170_out, OP5);
  not not_171 (not_171_out, OP4);
  not not_172 (not_172_out, OP2);
  not not_173 (not_173_out, OP0);
  not not_174 (not_174_out, OP5);
  not not_175 (not_175_out, OP4);
  not not_176 (not_176_out, OP1);
  not not_177 (not_177_out, OP4);
  not not_178 (not_178_out, OP3);
  not not_179 (not_179_out, OP2);
  not not_180 (not_180_out, OP5);
  not not_181 (not_181_out, OP4);
  not not_182 (not_182_out, OP3);
  not not_183 (not_183_out, OP2);
  not not_184 (not_184_out, OP1);
  not not_185 (not_185_out, OP0);
  not not_186 (not_186_out, F5);
  not not_187 (not_187_out, F4);
  not not_188 (not_188_out, F3);
  not not_189 (not_189_out, OP5);
  not not_190 (not_190_out, OP4);
  not not_191 (not_191_out, OP2);
  not not_192 (not_192_out, OP4);
  not not_193 (not_193_out, OP3);
  not not_194 (not_194_out, OP1);
  not not_195 (not_195_out, OP5);
  not not_196 (not_196_out, OP4);
  not not_197 (not_197_out, OP3);
  not not_198 (not_198_out, OP2);
  not not_199 (not_199_out, OP1);
  not not_200 (not_200_out, OP0);
  not not_201 (not_201_out, F5);
  not not_202 (not_202_out, F4);
  not not_203 (not_203_out, F1);
  not not_204 (not_204_out, F0);
  not not_205 (not_205_out, OP5);
  not not_206 (not_206_out, OP4);
  not not_207 (not_207_out, OP3);
  not not_208 (not_208_out, OP1);
  not not_209 (not_209_out, OP0);
  not not_210 (not_210_out, OP5);
  not not_211 (not_211_out, OP4);
  not not_212 (not_212_out, OP3);
  not not_213 (not_213_out, OP1);
  not not_214 (not_214_out, OP5);
  not not_215 (not_215_out, OP4);
  not not_216 (not_216_out, OP2);
  not not_217 (not_217_out, OP1);
  not not_218 (not_218_out, OP0);
  not not_219 (not_219_out, OP5);
  not not_220 (not_220_out, OP4);
  not not_221 (not_221_out, OP2);
  not not_222 (not_222_out, OP1);
  not not_223 (not_223_out, OP5);
  not not_224 (not_224_out, OP4);
  not not_225 (not_225_out, OP2);
  not not_226 (not_226_out, OP0);
  not not_227 (not_227_out, OP4);
  not not_228 (not_228_out, OP3);
  not not_229 (not_229_out, OP2);
  not not_230 (not_230_out, OP4);
  not not_231 (not_231_out, OP2);
  not not_232 (not_232_out, OP5);
  not not_233 (not_233_out, OP4);
  not not_234 (not_234_out, OP2);
  not not_235 (not_235_out, OP4);
  not not_236 (not_236_out, OP3);
  not not_237 (not_237_out, OP1);
  not not_238 (not_238_out, OP5);
  not not_239 (not_239_out, OP4);
  not not_240 (not_240_out, OP3);
  not not_241 (not_241_out, OP2);
  not not_242 (not_242_out, OP1);
  not not_243 (not_243_out, OP5);
  not not_244 (not_244_out, OP4);
  not not_245 (not_245_out, OP3);
  not not_246 (not_246_out, OP2);
  not not_247 (not_247_out, OP1);
  not not_248 (not_248_out, OP0);
  not not_249 (not_249_out, F5);
  not not_250 (not_250_out, F4);
  not not_251 (not_251_out, F3);
  not not_252 (not_252_out, F2);
  not not_253 (not_253_out, F1);
  not not_254 (not_254_out, F0);
  not not_255 (not_255_out, OP5);
  not not_256 (not_256_out, OP4);
  not not_257 (not_257_out, OP3);
  not not_258 (not_258_out, OP2);
  not not_259 (not_259_out, OP1);
  not not_260 (not_260_out, OP0);
  not not_261 (not_261_out, F5);
  not not_262 (not_262_out, F4);
  not not_263 (not_263_out, F3);
  not not_264 (not_264_out, F2);
  not not_265 (not_265_out, OP5);
  not not_266 (not_266_out, OP4);
  not not_267 (not_267_out, OP3);
  not not_268 (not_268_out, OP2);
  not not_269 (not_269_out, OP1);
  not not_270 (not_270_out, OP0);
  not not_271 (not_271_out, F5);
  not not_272 (not_272_out, F4);
  not not_273 (not_273_out, F3);
  not not_274 (not_274_out, F2);
  not not_275 (not_275_out, F0);
  not not_276 (not_276_out, OP5);
  not not_277 (not_277_out, OP4);
  not not_278 (not_278_out, OP3);
  not not_279 (not_279_out, OP2);
  not not_280 (not_280_out, OP1);
  not not_281 (not_281_out, OP0);
  not not_282 (not_282_out, F4);
  not not_283 (not_283_out, F3);
  not not_284 (not_284_out, F2);
  not not_285 (not_285_out, F1);
  not not_286 (not_286_out, F0);
  not not_287 (not_287_out, OP5);
  not not_288 (not_288_out, OP4);
  not not_289 (not_289_out, OP3);
  not not_290 (not_290_out, OP2);
  not not_291 (not_291_out, OP1);
  not not_292 (not_292_out, OP0);
  not not_293 (not_293_out, F4);
  not not_294 (not_294_out, F3);
  not not_295 (not_295_out, F2);
  not not_296 (not_296_out, F1);
  not not_297 (not_297_out, OP5);
  not not_298 (not_298_out, OP4);
  not not_299 (not_299_out, OP3);
  not not_300 (not_300_out, OP2);
  not not_301 (not_301_out, OP1);
  not not_302 (not_302_out, OP0);
  not not_303 (not_303_out, F4);
  not not_304 (not_304_out, F3);
  not not_305 (not_305_out, F2);
  not not_306 (not_306_out, F0);
  not not_307 (not_307_out, OP5);
  not not_308 (not_308_out, OP4);
  not not_309 (not_309_out, OP3);
  not not_310 (not_310_out, OP2);
  not not_311 (not_311_out, OP1);
  not not_312 (not_312_out, OP0);
  not not_313 (not_313_out, F4);
  not not_314 (not_314_out, F3);
  not not_315 (not_315_out, F1);
  not not_316 (not_316_out, F0);
  not not_317 (not_317_out, OP5);
  not not_318 (not_318_out, OP4);
  not not_319 (not_319_out, OP3);
  not not_320 (not_320_out, OP2);
  not not_321 (not_321_out, OP1);
  not not_322 (not_322_out, OP0);
  not not_323 (not_323_out, F4);
  not not_324 (not_324_out, F3);
  not not_325 (not_325_out, F1);
  not not_326 (not_326_out, OP5);
  not not_327 (not_327_out, OP4);
  not not_328 (not_328_out, OP3);
  not not_329 (not_329_out, OP2);
  not not_330 (not_330_out, OP1);
  not not_331 (not_331_out, OP0);
  not not_332 (not_332_out, F4);
  not not_333 (not_333_out, F3);
  not not_334 (not_334_out, OP5);
  not not_335 (not_335_out, OP4);
  not not_336 (not_336_out, OP3);
  not not_337 (not_337_out, OP2);
  not not_338 (not_338_out, OP1);
  not not_339 (not_339_out, OP0);
  not not_340 (not_340_out, F4);
  not not_341 (not_341_out, F2);
  not not_342 (not_342_out, F0);
  not not_343 (not_343_out, OP5);
  not not_344 (not_344_out, OP4);
  not not_345 (not_345_out, OP3);
  not not_346 (not_346_out, OP2);
  not not_347 (not_347_out, OP1);
  not not_348 (not_348_out, OP0);
  not not_349 (not_349_out, F4);
  not not_350 (not_350_out, F2);
  not not_351 (not_351_out, OP5);
  not not_352 (not_352_out, OP4);
  not not_353 (not_353_out, OP3);
  not not_354 (not_354_out, OP2);
  not not_355 (not_355_out, OP1);
  not not_356 (not_356_out, OP0);
  not not_357 (not_357_out, F5);
  not not_358 (not_358_out, F4);
  not not_359 (not_359_out, F2);
  not not_360 (not_360_out, F1);
  not not_361 (not_361_out, F0);
  not not_362 (not_362_out, OP5);
  not not_363 (not_363_out, OP4);
  not not_364 (not_364_out, OP3);
  not not_365 (not_365_out, OP2);
  not not_366 (not_366_out, OP1);
  not not_367 (not_367_out, OP0);
  not not_368 (not_368_out, F5);
  not not_369 (not_369_out, F4);
  not not_370 (not_370_out, F1);
  not not_371 (not_371_out, F0);
  not not_372 (not_372_out, OP5);
  not not_373 (not_373_out, OP4);
  not not_374 (not_374_out, OP3);
  not not_375 (not_375_out, OP2);
  not not_376 (not_376_out, OP1);
  not not_377 (not_377_out, OP0);
  not not_378 (not_378_out, F5);
  not not_379 (not_379_out, F4);
  not not_380 (not_380_out, F3);
  not not_381 (not_381_out, OP5);
  not not_382 (not_382_out, OP4);
  not not_383 (not_383_out, OP3);
  not not_384 (not_384_out, OP1);
  not not_385 (not_385_out, OP0);
  not not_386 (not_386_out, OP5);
  not not_387 (not_387_out, OP4);
  not not_388 (not_388_out, OP3);
  not not_389 (not_389_out, OP1);
  not not_390 (not_390_out, OP5);
  not not_391 (not_391_out, OP4);
  not not_392 (not_392_out, OP3);
  not not_393 (not_393_out, OP2);
  not not_394 (not_394_out, OP1);
  not not_395 (not_395_out, OP0);
  not not_396 (not_396_out, F5);
  not not_397 (not_397_out, F4);
  not not_398 (not_398_out, F2);
  not not_399 (not_399_out, F1);
  not not_400 (not_400_out, F0);
  not not_401 (not_401_out, OP5);
  not not_402 (not_402_out, OP4);
  not not_403 (not_403_out, OP3);
  not not_404 (not_404_out, OP2);
  not not_405 (not_405_out, OP1);
  not not_406 (not_406_out, OP0);
  not not_407 (not_407_out, F5);
  not not_408 (not_408_out, F4);
  not not_409 (not_409_out, F2);
  not not_410 (not_410_out, F1);
  not not_411 (not_411_out, F0);
  not not_412 (not_412_out, OP5);
  not not_413 (not_413_out, OP4);
  not not_414 (not_414_out, OP3);
  not not_415 (not_415_out, OP2);
  not not_416 (not_416_out, OP0);
  not not_417 (not_417_out, OP5);
  not not_418 (not_418_out, OP4);
  not not_419 (not_419_out, OP3);
  not not_420 (not_420_out, OP2);
  not not_421 (not_421_out, OP5);
  not not_422 (not_422_out, OP4);
  not not_423 (not_423_out, OP3);
  not not_424 (not_424_out, OP2);
  and and_1 (and_1_out, OP5, not_1_out, not_2_out, not_3_out, OP1, OP0);
  and and_2 (and_2_out, OP5, not_4_out, not_5_out, OP2, not_6_out, OP0);
  and and_3 (MemWrite, OP5, not_7_out, OP3, not_8_out, OP1, OP0);
  and and_4 (and_4_out, not_9_out, not_10_out, OP3, not_11_out, not_12_out, not_13_out);
  and and_5 (and_5_out, not_14_out, not_15_out, OP3, OP2, not_16_out, not_17_out);
  and and_6 (and_6_out, not_18_out, not_19_out, OP3, not_20_out, not_21_out, OP0);
  and and_7 (and_7_out, not_22_out, not_23_out, OP3, not_24_out, OP1, not_25_out);
  and and_8 (and_8_out, not_26_out, not_27_out, OP3, OP2, not_28_out, OP0);
  and and_9 (and_9_out, OP5, not_29_out, not_30_out, not_31_out, OP1, OP0);
  and and_10 (and_10_out, OP5, not_32_out, OP3, not_33_out, OP1, OP0);
  and and_11 (and_11_out, not_34_out, not_35_out, OP3, not_36_out, OP1, OP0);
  and and_12 (and_12_out, OP5, not_37_out, not_38_out, OP2, not_39_out, OP0);
  and and_13 (and_13_out, not_40_out, not_41_out, not_42_out, not_43_out, not_44_out, OP0);
  and and_14 (and_14_out, not_45_out, not_46_out, not_47_out, not_48_out, not_49_out, not_50_out, not_51_out, not_52_out, not_53_out, not_54_out, not_55_out, not_56_out);
  and and_15 (and_15_out, not_57_out, not_58_out, not_59_out, not_60_out, not_61_out, not_62_out, not_63_out, not_64_out, not_65_out, not_66_out, F1, F0);
  and and_16 (and_16_out, not_67_out, not_68_out, not_69_out, not_70_out, not_71_out, not_72_out, not_73_out, not_74_out, not_75_out, not_76_out, F1, not_77_out);
  and and_17 (and_17_out, not_78_out, not_79_out, not_80_out, not_81_out, not_82_out, not_83_out, F5, not_84_out, not_85_out, not_86_out, not_87_out, not_88_out);
  and and_18 (and_18_out, not_89_out, not_90_out, not_91_out, not_92_out, not_93_out, not_94_out, F5, not_95_out, not_96_out, not_97_out, not_98_out, F0);
  and and_19 (and_19_out, not_99_out, not_100_out, not_101_out, not_102_out, not_103_out, not_104_out, F5, not_105_out, not_106_out, not_107_out, F1, not_108_out);
  and and_20 (and_20_out, not_109_out, not_110_out, not_111_out, not_112_out, not_113_out, not_114_out, F5, not_115_out, not_116_out, F2, not_117_out, not_118_out);
  and and_21 (and_21_out, not_119_out, not_120_out, not_121_out, not_122_out, not_123_out, not_124_out, F5, not_125_out, not_126_out, F2, not_127_out, F0);
  and and_22 (and_22_out, not_128_out, not_129_out, not_130_out, not_131_out, not_132_out, not_133_out, F5, not_134_out, not_135_out, F2, F1, F0);
  and and_23 (and_23_out, not_136_out, not_137_out, not_138_out, not_139_out, not_140_out, not_141_out, F5, not_142_out, F3, not_143_out, F1, not_144_out);
  and and_24 (and_24_out, not_145_out, not_146_out, not_147_out, not_148_out, not_149_out, not_150_out, F5, not_151_out, F3, not_152_out, F1, F0);
  and and_25 (and_25_out, not_153_out, not_154_out, not_155_out, not_156_out, OP1, OP0);
  and and_26 (and_26_out, not_157_out, not_158_out, OP3, not_159_out, not_160_out, not_161_out);
  and and_27 (and_27_out, not_162_out, not_163_out, OP3, OP2, not_164_out, not_165_out);
  and and_28 (and_28_out, not_166_out, not_167_out, OP3, not_168_out, not_169_out, OP0);
  and and_29 (and_29_out, not_170_out, not_171_out, OP3, not_172_out, OP1, not_173_out);
  and and_30 (and_30_out, not_174_out, not_175_out, OP3, OP2, not_176_out, OP0);
  and and_31 (and_31_out, OP5, not_177_out, not_178_out, not_179_out, OP1, OP0);
  and and_32 (and_32_out, not_180_out, not_181_out, not_182_out, not_183_out, not_184_out, not_185_out, not_186_out, not_187_out, not_188_out, F2, F1, F0);
  and and_33 (and_33_out, not_189_out, not_190_out, OP3, not_191_out, OP1, OP0);
  and and_34 (and_34_out, OP5, not_192_out, not_193_out, OP2, not_194_out, OP0);
  and and_35 (SysCALL, not_195_out, not_196_out, not_197_out, not_198_out, not_199_out, not_200_out, not_201_out, not_202_out, F3, F2, not_203_out, not_204_out);
  and and_36 (and_36_out, not_205_out, not_206_out, not_207_out, OP2, not_208_out, not_209_out);
  and and_37 (and_37_out, not_210_out, not_211_out, not_212_out, OP2, not_213_out, OP0);
  and and_38 (and_38_out, not_214_out, not_215_out, OP3, not_216_out, not_217_out, not_218_out);
  and and_39 (and_39_out, not_219_out, not_220_out, OP3, not_221_out, not_222_out, OP0);
  and and_40 (and_40_out, not_223_out, not_224_out, OP3, not_225_out, OP1, not_226_out);
  and and_41 (and_41_out, OP5, not_227_out, not_228_out, not_229_out, OP1, OP0);
  and and_42 (and_42_out, OP5, not_230_out, OP3, not_231_out, OP1, OP0);
  and and_43 (and_43_out, not_232_out, not_233_out, OP3, not_234_out, OP1, OP0);
  and and_44 (and_44_out, OP5, not_235_out, not_236_out, OP2, not_237_out, OP0);
  and and_45 (and_45_out, not_238_out, not_239_out, not_240_out, not_241_out, not_242_out, OP0);
  and and_46 (and_46_out, not_243_out, not_244_out, not_245_out, not_246_out, not_247_out, not_248_out, not_249_out, not_250_out, not_251_out, not_252_out, not_253_out, not_254_out);
  and and_47 (and_47_out, not_255_out, not_256_out, not_257_out, not_258_out, not_259_out, not_260_out, not_261_out, not_262_out, not_263_out, not_264_out, F1, F0);
  and and_48 (and_48_out, not_265_out, not_266_out, not_267_out, not_268_out, not_269_out, not_270_out, not_271_out, not_272_out, not_273_out, not_274_out, F1, not_275_out);
  and and_49 (and_49_out, not_276_out, not_277_out, not_278_out, not_279_out, not_280_out, not_281_out, F5, not_282_out, not_283_out, not_284_out, not_285_out, not_286_out);
  and and_50 (and_50_out, not_287_out, not_288_out, not_289_out, not_290_out, not_291_out, not_292_out, F5, not_293_out, not_294_out, not_295_out, not_296_out, F0);
  and and_51 (and_51_out, not_297_out, not_298_out, not_299_out, not_300_out, not_301_out, not_302_out, F5, not_303_out, not_304_out, not_305_out, F1, not_306_out);
  and and_52 (and_52_out, not_307_out, not_308_out, not_309_out, not_310_out, not_311_out, not_312_out, F5, not_313_out, not_314_out, F2, not_315_out, not_316_out);
  and and_53 (and_53_out, not_317_out, not_318_out, not_319_out, not_320_out, not_321_out, not_322_out, F5, not_323_out, not_324_out, F2, not_325_out, F0);
  and and_54 (and_54_out, not_326_out, not_327_out, not_328_out, not_329_out, not_330_out, not_331_out, F5, not_332_out, not_333_out, F2, F1, F0);
  and and_55 (and_55_out, not_334_out, not_335_out, not_336_out, not_337_out, not_338_out, not_339_out, F5, not_340_out, F3, not_341_out, F1, not_342_out);
  and and_56 (and_56_out, not_343_out, not_344_out, not_345_out, not_346_out, not_347_out, not_348_out, F5, not_349_out, F3, not_350_out, F1, F0);
  and and_57 (and_57_out, not_351_out, not_352_out, not_353_out, not_354_out, not_355_out, not_356_out, not_357_out, not_358_out, F3, not_359_out, not_360_out, not_361_out);
  and and_58 (and_58_out, not_362_out, not_363_out, not_364_out, not_365_out, not_366_out, not_367_out, not_368_out, not_369_out, F3, F2, not_370_out, not_371_out);
  and and_59 (and_59_out, not_372_out, not_373_out, not_374_out, not_375_out, not_376_out, not_377_out, not_378_out, not_379_out, not_380_out, F2, F1, F0);
  and and_60 (BEQ, not_381_out, not_382_out, not_383_out, OP2, not_384_out, not_385_out);
  and and_61 (BNE, not_386_out, not_387_out, not_388_out, OP2, not_389_out, OP0);
  and and_62 (JR, not_390_out, not_391_out, not_392_out, not_393_out, not_394_out, not_395_out, not_396_out, not_397_out, F3, not_398_out, not_399_out, not_400_out);
  and and_63 (and_63_out, not_401_out, not_402_out, not_403_out, not_404_out, not_405_out, not_406_out, not_407_out, not_408_out, F3, not_409_out, not_410_out, not_411_out);
  and and_64 (and_64_out, not_412_out, not_413_out, not_414_out, not_415_out, OP1, not_416_out);
  and and_65 (and_65_out, not_417_out, not_418_out, not_419_out, not_420_out, OP1, OP0);
  and and_66 (JAL, not_421_out, not_422_out, not_423_out, not_424_out, OP1, OP0);
  or or_1 (MemToReg, and_1_out, and_2_out);
  or or_2 (ALU_SRC, and_4_out, and_5_out, and_6_out, and_7_out, and_8_out, and_9_out, and_10_out, and_11_out, and_12_out, and_13_out);
  or or_3 (SignedExt, and_36_out, and_37_out, and_38_out, and_39_out, and_40_out, and_41_out, and_42_out, and_43_out, and_44_out, and_45_out);
  or or_4 (JMP, and_63_out, and_64_out, and_65_out);
  or or_5 (RegWrite, and_14_out, and_15_out, and_16_out, and_17_out, and_18_out, and_19_out, and_20_out, and_21_out, and_22_out, and_23_out, and_24_out, and_25_out, and_26_out, and_27_out, and_28_out, and_29_out, and_30_out, and_31_out, and_32_out, and_33_out, and_34_out);
  or or_6 (RegDst, and_46_out, and_47_out, and_48_out, and_49_out, and_50_out, and_51_out, and_52_out, and_53_out, and_54_out, and_55_out, and_56_out, and_57_out, and_58_out, and_59_out);
endmodule

// ALU
module MIPS_ALU (
  input  [4:0] shamt,
  input  [31:0] X,
  input  [31:0] Y,
  input  [3:0] AluOP,
  output Equal,
  output [31:0] Result,
  output [31:0] Result_2
);

  wire [0:0] comparator_1_lt, comparator_2_lt;
  wire [31:0] adder_1_out, AND_out, divider_1_out, divider_1_rem, multiplier_1_cout, multiplier_1_out,
       NOR_out, OR_out, shifter_1_out, shifter_2_out, shifter_3_out, subtractor_1_out, XOR_out;

  assign AND_out = X & Y;  // AND_Gate AND, 32 bits wide
  assign OR_out = X | Y;  // OR_Gate OR, 32 bits wide
  Shifter #(.width(32)) shifter_1 (.in(Y), .\dist (shamt), .out(shifter_1_out));
  Shifter #(.width(32), .shift("ar")) shifter_2 (.in(Y), .\dist (shamt), .out(shifter_2_out));
  Shifter #(.width(32), .shift("lr")) shifter_3 (.in(Y), .\dist (shamt), .out(shifter_3_out));
  Multiplier #(.width(32)) multiplier_1 (.a(X), .b(Y), .out(multiplier_1_out), .cout(multiplier_1_cout));  // open: cin
  Divider #(.width(32)) divider_1 (.a(X), .b(Y), .out(divider_1_out), .rem(divider_1_rem));  // open: upper
  Adder #(.width(32)) adder_1 (.a(X), .b(Y), .out(adder_1_out));  // open: cin, cout
  Subtractor #(.width(32)) subtractor_1 (.a(X), .b(Y), .out(subtractor_1_out));  // open: bin, bout
  assign XOR_out = X ^ Y;  // XOR_Gate XOR, 32 bits wide
  assign NOR_out = ~(X | Y);  // NOR_Gate NOR, 32 bits wide
  Comparator #(.width(32)) comparator_1 (.a(X), .b(Y), .eq(Equal), .lt(comparator_1_lt[0]));  // open: gt
  Comparator #(.width(32), .mode("unsigned")) comparator_2 (.a(X), .b(Y), .lt(comparator_2_lt[0]));  // open: gt, eq
  Multiplexer #(.select(4), .width(32), .enable("false")) multiplexer_1 (
    .in0(shifter_1_out), .in1(shifter_2_out), .in2(shifter_3_out), .in3(multiplier_1_out),
    .in4(divider_1_out), .in5(adder_1_out), .in6(subtractor_1_out), .in7(AND_out), .in8(OR_out),
    .in9(XOR_out), .in10(NOR_out), .in11({{31{1'b0}}, comparator_1_lt[0]}),
    .in12({{31{1'b0}}, comparator_2_lt[0]}), .in13({32{1'b0}}), .in14({32{1'b0}}), .in15({32{1'b0}}),
    .out(Result), .sel(AluOP));
  Multiplexer #(.select(4), .width(32), .enable("false")) multiplexer_2 (
    .in0({32{1'b0}}), .in1({32{1'b0}}), .in2({32{1'b0}}), .in3(multiplier_1_cout), .in4(divider_1_rem),
    .in5({32{1'b0}}), .in6({32{1'b0}}), .in7({32{1'b0}}), .in8({32{1'b0}}), .in9({32{1'b0}}),
    .in10({32{1'b0}}), .in11({32{1'b0}}), .in12({32{1'b0}}), .in13({32{1'b0}}), .in14({32{1'b0}}),
    .in15({32{1'b0}}), .out(Result_2), .sel(AluOP));

  // Other names for the same wires on the sheet: Result2[31:0] = Result_2; S[3:0] = AluOP

  // Notes on the sheet:
  //   不要改变此引脚区域内容，也不要改变ALU封装形式
  //   输入引脚
  //   输出引脚
endmodule

module MIPS_Regifile (
  input  [31:0] Din,
  input  Clk,
  input  WE,
  input  [4:0] R1_num,
  input  [4:0] W_num,
  input  [4:0] R2_num,
  output [31:0] R1,
  output [31:0] R2
);

  // RegisterFile registerfile_1: pin names not known; wires that end beside it: Din, Clk, WE, W_num, R1_num, R2_num, R1, R2
endmodule

module \理想流水线  (
);

  wire and_1_out, and_2_out, BGEZ, CLK, comparator_1_eq, EX_MEM_p12, EX_MEM_p13, EX_MEM_p14, EX_MEM_p15,
       EX_MEM_p17, EX_MEM_p20, Go, ID_EX_p15, ID_EX_p18, ID_EX_p19, ID_EX_p20, ID_EX_p21, ID_EX_p23,
       ID_EX_p25, ID_EX_p30, IR1, IR2, IR3, JAL, JMP, JR, LHU, MEM_WB_p12, not_1_out, or_1_out, RegDst,
       RegWrite, RST, SignedExt, SLTIU, SRAV, Sys_out, Syscall, W1, W2, W3, \暂停 , \硬布线控制器_1_alu_src ,
       \硬布线控制器_1_memtoreg , \硬布线控制器_1_memwrite , \硬布线控制器_1_regwrite ;
  wire [3:0] ID_EX_p22, \硬布线控制器_1_alu_op ;
  wire [4:0] ID_EX_p29, MEM_WB_p17, multiplexer_1_out, multiplexer_2_out, multiplexer_3_out,
       multiplexer_5_out;
  wire [15:0] \LoadUse次数 , \总周期数 , \插入气泡数 , \无条件分支数 , \条件分支成功数 ;
  wire [31:0] bit_extender_1_out, bit_extender_2_out, EX_MEM_p18, EX_MEM_p19, EX_PC, ID_EX_p26, ID_EX_p27,
       ID_EX_p28, ID_PC, IF_PC, IR, LedData, MEM_PC, MEM_WB_p15, MEM_WB_p16, mips_alu_1_result,
       multiplexer_4_out, multiplexer_6_out, multiplexer_7_out, PC_q, R1, R2, ram_1_data, rom_1_data,
       shifter_1_out, WB_PC, \条件分支跳转地址 ;

  Button \u_总复位  (.out(RST));
  Button _1 (.out(IR1));
  Button _2 (.out(IR2));
  Button _3 (.out(IR3));
  Button \u_继续运行  (.out(Go));
  LED led_1 (.in(W1));
  LED led_2 (.in(W2));
  LED led_3 (.in(W3));
  Hex_Digit_Display hex_digit_display_1 (.value(LedData[31:28]));  // open: dp
  Comparator #(.width(32)) comparator_1 (.a(R1), .b(32'h22), .eq(comparator_1_eq));  // open: gt, lt
  Hex_Digit_Display hex_digit_display_2 (.value(LedData[23:20]));  // open: dp
  Hex_Digit_Display hex_digit_display_3 (.value(LedData[27:24]));  // open: dp
  Register #(.width(32)) PC (.D(IF_PC), .en(\暂停 ), .Q(PC_q), .clk(CLK), .clr(RST));
  and and_1 (and_1_out, comparator_1_eq, Sys_out);
  and and_2 (and_2_out, ~comparator_1_eq, Sys_out);  // AND_Gate
  Hex_Digit_Display hex_digit_display_4 (.value(LedData[19:16]));  // open: dp
  Hex_Digit_Display hex_digit_display_5 (.value(LedData[15:12]));  // open: dp
  Adder #(.width(32)) adder_1 (.a(PC_q), .b(32'h4), .out(IF_PC));  // open: cin, cout
  Register #(.width(32)) register_1 (.D(R2), .en(and_1_out), .Q(LedData), .clk(CLK), .clr(RST));
  D_Flip_Flop d_ff_1 (.clk(CLK), .D(and_2_out), .Qn(\暂停 ), .preset(1'b0), .en(\暂停 ), .reset(or_1_out));  // open: Q
  or or_1 (or_1_out, RST, Go);
  Hex_Digit_Display hex_digit_display_6 (.value(LedData[7:4]));  // open: dp
  Hex_Digit_Display hex_digit_display_7 (.value(LedData[11:8]));  // open: dp
  Clock clock_1 (.out(CLK));
  ROM #(.addrWidth(10), .dataWidth(32)) rom_1 (.addr(PC_q[11:2]), .data(rom_1_data));  // open: sel
  Hex_Digit_Display hex_digit_display_8 (.value(LedData[3:0]));  // open: dp
  IF_ID IF_ID (
    .PC_in(IF_PC), .Instruction_in(rom_1_data), .PC_out(ID_PC), .Instruction_out(IR), .\同步清零端_高电平有效 (RST),
    .CLK(CLK));  // open: 使能端_低电平有效, Reset
  Counter #(.width(16), .max('hffff)) counter_1 (
    .count(\暂停 ), .Q(\总周期数 ), .clk(CLK), .clr(RST));  // open: load, D, carry
  // Probe on \总周期数 
  // Probe on \无条件分支数 
  // Probe on \条件分支成功数 
  // Probe on \插入气泡数 
  // Probe on \LoadUse次数 
  // Probe on IF_PC[11:0]
  Multiplexer #(.width(5), .enable("false")) multiplexer_1 (
    .in0(IR[25:21]), .in1(5'b00010), .out(multiplexer_1_out), .sel(Sys_out));
  Multiplexer #(.width(5), .enable("false")) multiplexer_2 (
    .in0(IR[20:16]), .in1(5'b00100), .out(multiplexer_2_out), .sel(Sys_out));
  assign bit_extender_1_out = {{16{1'b0}}, IR[15:0]};  // Bit_Extender bit_extender_1
  assign bit_extender_2_out = {{16{IR[15]}}, IR[15:0]};  // Bit_Extender bit_extender_2
  // Probe on ID_PC[11:0]
  Multiplexer #(.width(5), .enable("false")) multiplexer_3 (
    .in0(IR[20:16]), .in1(IR[15:11]), .out(multiplexer_3_out), .sel(RegDst));
  Multiplexer #(.width(32), .enable("false")) multiplexer_4 (
    .in0(bit_extender_1_out), .in1(bit_extender_2_out), .out(multiplexer_4_out), .sel(SignedExt));
  // Probe on EX_PC[11:0]
  // Probe on MEM_PC[11:0]
  \硬布线控制器  \u_硬布线控制器_1  (
    .Func(IR[5:0]), .OP(IR[31:26]), .ALU_OP(\硬布线控制器_1_alu_op ), .MemToReg(\硬布线控制器_1_memtoreg ),
    .MemWrite(\硬布线控制器_1_memwrite ), .ALU_SRC(\硬布线控制器_1_alu_src ), .RegWrite(\硬布线控制器_1_regwrite ),
    .SysCALL(Syscall), .SignedExt(SignedExt), .RegDst(RegDst), .JR(JR), .JMP(JMP), .JAL(JAL), .LHU(LHU),
    .BGEZ(BGEZ), .SLTIU(SLTIU), .SRAV(SRAV));  // open: Beq, Bne
  Multiplexer #(.width(5), .enable("false")) multiplexer_5 (
    .in0(multiplexer_3_out), .in1({5{1'b1}}), .out(multiplexer_5_out), .sel(JAL));
  // Probe on WB_PC[11:0]
  MIPS_Regifile mips_regifile_1 (
    .Din(multiplexer_7_out), .Clk(CLK), .R1(R1), .R2(R2), .WE(RegWrite), .W_num(MEM_WB_p17),
    .R1_num(multiplexer_1_out), .R2_num(multiplexer_2_out));
  // ID_EX ID_EX: pin names not known; wires that end beside it: Syscall, \硬布线控制器_1_memtoreg , \硬布线控制器_1_regwrite , \硬布线控制器_1_memwrite , \硬布线控制器_1_alu_op , \硬布线控制器_1_alu_src , ID_PC, IR, R1, R2, multiplexer_4_out, IR[10:6], multiplexer_5_out, RST, ID_EX_p15, ID_EX_p15, CLK, ID_EX_p18, ID_EX_p19, ID_EX_p20, ID_EX_p21, ID_EX_p22, ID_EX_p23, EX_PC, ID_EX_p25, ID_EX_p26, ID_EX_p27, ID_EX_p28, ID_EX_p29, ID_EX_p30
  Multiplexer #(.width(32), .enable("false")) multiplexer_6 (
    .in0(ID_EX_p27), .in1(ID_EX_p28), .out(multiplexer_6_out), .sel(ID_EX_p23));
  Shifter #(.width(32)) shifter_1 (.in(ID_EX_p28), .\dist (5'b00010), .out(shifter_1_out));
  MIPS_ALU mips_alu_1 (
    .X(ID_EX_p26), .Y(multiplexer_6_out), .AluOP(ID_EX_p22), .Result(mips_alu_1_result), .shamt(ID_EX_p29));  // open: Equal, Result_2
  Adder #(.width(32)) adder_2 (.a(shifter_1_out), .b(EX_PC), .out(\条件分支跳转地址 ));  // open: cin, cout
  // EX_MEM EX_MEM: pin names not known; wires that end beside it: ID_EX_p18, ID_EX_p19, ID_EX_p20, ID_EX_p21, EX_PC, ID_EX_p25, ID_EX_p27, mips_alu_1_result, ID_EX_p30, RST, CLK, EX_MEM_p12, EX_MEM_p13, EX_MEM_p14, EX_MEM_p15, MEM_PC, EX_MEM_p17, EX_MEM_p18, EX_MEM_p19, EX_MEM_p20
  RAM #(.addrWidth(10), .dataWidth(32), .bus("separate")) ram_1 (
    .addr(EX_MEM_p19[11:2]), .din(EX_MEM_p18), .data(ram_1_data), .str(EX_MEM_p15), .clk(CLK),
    .ld(not_1_out), .clr(RST));  // open: sel
  not not_1 (not_1_out, EX_MEM_p15);
  // MEM_WB MEM_WB: pin names not known; wires that end beside it: EX_MEM_p12, EX_MEM_p13, EX_MEM_p14, MEM_PC, EX_MEM_p17, EX_MEM_p19, ram_1_data, EX_MEM_p20, RST, CLK, Sys_out, MEM_WB_p12, RegWrite, WB_PC, MEM_WB_p15, MEM_WB_p16, MEM_WB_p17
  Multiplexer #(.width(32), .enable("false")) multiplexer_7 (
    .in0(MEM_WB_p15), .in1(MEM_WB_p16), .out(multiplexer_7_out), .sel(MEM_WB_p12));

  // Other names for the same wires on the sheet: PC_4[31:0] = ID_PC

  // Notes on the sheet:
  //   中断源
  //   中断等待指示
  //   数码管输出
  //   指令存储器
  //   contents of rom_1 (hex, n*v repeats v):
  //   20100000 20110001 20120002 20130003 36100000 36310001 36520002 36730003 ae100000 ae110004 ae120008
  //   ae13000c 2002000a 0 0 0 c
  //   指令字
  //   OP
  //   rs
  //   rt
  //   rd
  //   imm
  //   JMP
  //   JR
  //   SRAV
  //   SLTIU
  //   LHU
  //   BGEZ
  //   OP
  //   Func
  //   流水调试日志用
  //   Beq
  //   Bne
  //   MemToReg
  //   MemWrite
  //   AluOP
  //   AluSrcB
  //   RegWrite
  //   JAL
  //   RegDst
endmodule

// 源寄存器使用情况
module \源寄存器使用情况  (
  input  OP0,
  input  OP1,
  input  OP2,
  input  OP3,
  input  OP4,
  input  OP5,
  input  F0,
  input  F1,
  input  F2,
  input  F3,
  input  F4,
  input  F5,
  output R1_Used,
  output R2_Used
);

  wire and_1_out, and_2_out, and_3_out, and_4_out, and_5_out, and_6_out, and_7_out, and_8_out, and_9_out,
       and_10_out, and_11_out, and_12_out, and_13_out, and_14_out, and_15_out, and_16_out, and_17_out,
       and_18_out, and_19_out, and_20_out, and_21_out, and_22_out, and_23_out, and_24_out, and_25_out,
       and_26_out, and_27_out, and_28_out, and_29_out, and_30_out, and_31_out, and_32_out, and_33_out,
       and_34_out, and_35_out, and_36_out, and_37_out, and_38_out, and_39_out, not_1_out, not_2_out,
       not_3_out, not_4_out, not_5_out, not_6_out, not_7_out, not_8_out, not_9_out, not_10_out, not_11_out,
       not_12_out, not_13_out, not_14_out, not_15_out, not_16_out, not_17_out, not_18_out, not_19_out,
       not_20_out, not_21_out, not_22_out, not_23_out, not_24_out, not_25_out, not_26_out, not_27_out,
       not_28_out, not_29_out, not_30_out, not_31_out, not_32_out, not_33_out, not_34_out, not_35_out,
       not_36_out, not_37_out, not_38_out, not_39_out, not_40_out, not_41_out, not_42_out, not_43_out,
       not_44_out, not_45_out, not_46_out, not_47_out, not_48_out, not_49_out, not_50_out, not_51_out,
       not_52_out, not_53_out, not_54_out, not_55_out, not_56_out, not_57_out, not_58_out, not_59_out,
       not_60_out, not_61_out, not_62_out, not_63_out, not_64_out, not_65_out, not_66_out, not_67_out,
       not_68_out, not_69_out, not_70_out, not_71_out, not_72_out, not_73_out, not_74_out, not_75_out,
       not_76_out, not_77_out, not_78_out, not_79_out, not_80_out, not_81_out, not_82_out, not_83_out,
       not_84_out, not_85_out, not_86_out, not_87_out, not_88_out, not_89_out, not_90_out, not_91_out,
       not_92_out, not_93_out, not_94_out, not_95_out, not_96_out, not_97_out, not_98_out, not_99_out,
       not_100_out, not_101_out, not_102_out, not_103_out, not_104_out, not_105_out, not_106_out,
       not_107_out, not_108_out, not_109_out, not_110_out, not_111_out, not_112_out, not_113_out,
       not_114_out, not_115_out, not_116_out, not_117_out, not_118_out, not_119_out, not_120_out,
       not_121_out, not_122_out, not_123_out, not_124_out, not_125_out, not_126_out, not_127_out,
       not_128_out, not_129_out, not_130_out, not_131_out, not_132_out, not_133_out, not_134_out,
       not_135_out, not_136_out, not_137_out, not_138_out, not_139_out, not_140_out, not_141_out,
       not_142_out, not_143_out, not_144_out, not_145_out, not_146_out, not_147_out, not_148_out,
       not_149_out, not_150_out, not_151_out, not_152_out, not_153_out, not_154_out, not_155_out,
       not_156_out, not_157_out, not_158_out, not_159_out, not_160_out, not_161_out, not_162_out,
       not_163_out, not_164_out, not_165_out, not_166_out, not_167_out, not_168_out, not_169_out,
       not_170_out, not_171_out, not_172_out, not_173_out, not_174_out, not_175_out, not_176_out,
       not_177_out, not_178_out, not_179_out, not_180_out, not_181_out, not_182_out, not_183_out,
       not_184_out, not_185_out, not_186_out, not_187_out, not_188_out, not_189_out, not_190_out,
       not_191_out, not_192_out, not_193_out, not_194_out, not_195_out, not_196_out, not_197_out,
       not_198_out, not_199_out, not_200_out, not_201_out, not_202_out, not_203_out, not_204_out,
       not_205_out, not_206_out, not_207_out, not_208_out, not_209_out, not_210_out, not_211_out,
       not_212_out, not_213_out, not_214_out, not_215_out, not_216_out, not_217_out, not_218_out,
       not_219_out, not_220_out, not_221_out, not_222_out, not_223_out, not_224_out, not_225_out,
       not_226_out, not_227_out, not_228_out, not_229_out, not_230_out, not_231_out, not_232_out,
       not_233_out, not_234_out, not_235_out, not_236_out, not_237_out, not_238_out, not_239_out,
       not_240_out, not_241_out, not_242_out, not_243_out, not_244_out, not_245_out, not_246_out,
       not_247_out, not_248_out, not_249_out, not_250_out, not_251_out, not_252_out, not_253_out,
       not_254_out, not_255_out, not_256_out, not_257_out, not_258_out, not_259_out, not_260_out,
       not_261_out, not_262_out, not_263_out, not_264_out, not_265_out, not_266_out, not_267_out,
       not_268_out, not_269_out, not_270_out, not_271_out, not_272_out, not_273_out, not_274_out,
       not_275_out, not_276_out, not_277_out, not_278_out, not_279_out, not_280_out, not_281_out,
       not_282_out, not_283_out, not_284_out, not_285_out, not_286_out, not_287_out, not_288_out;

  not not_1 (not_1_out, OP5);
  not not_2 (not_2_out, OP4);
  not not_3 (not_3_out, OP3);
  not not_4 (not_4_out, OP2);
  not not_5 (not_5_out, OP1);
  not not_6 (not_6_out, OP0);
  not not_7 (not_7_out, F4);
  not not_8 (not_8_out, F3);
  not not_9 (not_9_out, F2);
  not not_10 (not_10_out, F1);
  not not_11 (not_11_out, F0);
  not not_12 (not_12_out, OP5);
  not not_13 (not_13_out, OP4);
  not not_14 (not_14_out, OP3);
  not not_15 (not_15_out, OP2);
  not not_16 (not_16_out, OP1);
  not not_17 (not_17_out, OP0);
  not not_18 (not_18_out, F4);
  not not_19 (not_19_out, F3);
  not not_20 (not_20_out, F2);
  not not_21 (not_21_out, F1);
  not not_22 (not_22_out, OP5);
  not not_23 (not_23_out, OP4);
  not not_24 (not_24_out, OP3);
  not not_25 (not_25_out, OP2);
  not not_26 (not_26_out, OP1);
  not not_27 (not_27_out, OP0);
  not not_28 (not_28_out, F4);
  not not_29 (not_29_out, F3);
  not not_30 (not_30_out, F2);
  not not_31 (not_31_out, F0);
  not not_32 (not_32_out, OP5);
  not not_33 (not_33_out, OP4);
  not not_34 (not_34_out, OP3);
  not not_35 (not_35_out, OP2);
  not not_36 (not_36_out, OP1);
  not not_37 (not_37_out, OP0);
  not not_38 (not_38_out, F4);
  not not_39 (not_39_out, F3);
  not not_40 (not_40_out, F1);
  not not_41 (not_41_out, F0);
  not not_42 (not_42_out, OP5);
  not not_43 (not_43_out, OP4);
  not not_44 (not_44_out, OP3);
  not not_45 (not_45_out, OP2);
  not not_46 (not_46_out, OP1);
  not not_47 (not_47_out, OP0);
  not not_48 (not_48_out, F4);
  not not_49 (not_49_out, F3);
  not not_50 (not_50_out, F1);
  not not_51 (not_51_out, OP5);
  not not_52 (not_52_out, OP4);
  not not_53 (not_53_out, OP3);
  not not_54 (not_54_out, OP2);
  not not_55 (not_55_out, OP1);
  not not_56 (not_56_out, OP0);
  not not_57 (not_57_out, F4);
  not not_58 (not_58_out, F3);
  not not_59 (not_59_out, OP5);
  not not_60 (not_60_out, OP4);
  not not_61 (not_61_out, OP3);
  not not_62 (not_62_out, OP2);
  not not_63 (not_63_out, OP1);
  not not_64 (not_64_out, OP0);
  not not_65 (not_65_out, F4);
  not not_66 (not_66_out, F2);
  not not_67 (not_67_out, F0);
  not not_68 (not_68_out, OP5);
  not not_69 (not_69_out, OP4);
  not not_70 (not_70_out, OP3);
  not not_71 (not_71_out, OP2);
  not not_72 (not_72_out, OP1);
  not not_73 (not_73_out, OP0);
  not not_74 (not_74_out, F4);
  not not_75 (not_75_out, F2);
  not not_76 (not_76_out, OP5);
  not not_77 (not_77_out, OP4);
  not not_78 (not_78_out, OP3);
  not not_79 (not_79_out, OP2);
  not not_80 (not_80_out, OP1);
  not not_81 (not_81_out, OP0);
  not not_82 (not_82_out, F5);
  not not_83 (not_83_out, F4);
  not not_84 (not_84_out, F2);
  not not_85 (not_85_out, F1);
  not not_86 (not_86_out, F0);
  not not_87 (not_87_out, OP5);
  not not_88 (not_88_out, OP4);
  not not_89 (not_89_out, OP3);
  not not_90 (not_90_out, OP2);
  not not_91 (not_91_out, OP1);
  not not_92 (not_92_out, OP0);
  not not_93 (not_93_out, F5);
  not not_94 (not_94_out, F4);
  not not_95 (not_95_out, F1);
  not not_96 (not_96_out, F0);
  not not_97 (not_97_out, OP5);
  not not_98 (not_98_out, OP4);
  not not_99 (not_99_out, OP3);
  not not_100 (not_100_out, OP1);
  not not_101 (not_101_out, OP0);
  not not_102 (not_102_out, OP5);
  not not_103 (not_103_out, OP4);
  not not_104 (not_104_out, OP3);
  not not_105 (not_105_out, OP1);
  not not_106 (not_106_out, OP5);
  not not_107 (not_107_out, OP4);
  not not_108 (not_108_out, OP2);
  not not_109 (not_109_out, OP1);
  not not_110 (not_110_out, OP0);
  not not_111 (not_111_out, OP5);
  not not_112 (not_112_out, OP4);
  not not_113 (not_113_out, OP1);
  not not_114 (not_114_out, OP0);
  not not_115 (not_115_out, OP5);
  not not_116 (not_116_out, OP4);
  not not_117 (not_117_out, OP2);
  not not_118 (not_118_out, OP1);
  not not_119 (not_119_out, OP5);
  not not_120 (not_120_out, OP4);
  not not_121 (not_121_out, OP2);
  not not_122 (not_122_out, OP0);
  not not_123 (not_123_out, OP5);
  not not_124 (not_124_out, OP4);
  not not_125 (not_125_out, OP1);
  not not_126 (not_126_out, OP4);
  not not_127 (not_127_out, OP3);
  not not_128 (not_128_out, OP2);
  not not_129 (not_129_out, OP4);
  not not_130 (not_130_out, OP2);
  not not_131 (not_131_out, OP5);
  not not_132 (not_132_out, OP4);
  not not_133 (not_133_out, OP3);
  not not_134 (not_134_out, OP2);
  not not_135 (not_135_out, OP1);
  not not_136 (not_136_out, OP0);
  not not_137 (not_137_out, F5);
  not not_138 (not_138_out, F4);
  not not_139 (not_139_out, F3);
  not not_140 (not_140_out, OP5);
  not not_141 (not_141_out, OP4);
  not not_142 (not_142_out, OP2);
  not not_143 (not_143_out, OP4);
  not not_144 (not_144_out, OP3);
  not not_145 (not_145_out, OP1);
  not not_146 (not_146_out, OP5);
  not not_147 (not_147_out, OP4);
  not not_148 (not_148_out, OP3);
  not not_149 (not_149_out, OP2);
  not not_150 (not_150_out, OP1);
  not not_151 (not_151_out, OP5);
  not not_152 (not_152_out, OP4);
  not not_153 (not_153_out, OP3);
  not not_154 (not_154_out, OP2);
  not not_155 (not_155_out, OP1);
  not not_156 (not_156_out, OP0);
  not not_157 (not_157_out, F5);
  not not_158 (not_158_out, F4);
  not not_159 (not_159_out, F3);
  not not_160 (not_160_out, F2);
  not not_161 (not_161_out, F1);
  not not_162 (not_162_out, F0);
  not not_163 (not_163_out, OP5);
  not not_164 (not_164_out, OP4);
  not not_165 (not_165_out, OP3);
  not not_166 (not_166_out, OP2);
  not not_167 (not_167_out, OP1);
  not not_168 (not_168_out, OP0);
  not not_169 (not_169_out, F5);
  not not_170 (not_170_out, F4);
  not not_171 (not_171_out, F3);
  not not_172 (not_172_out, F2);
  not not_173 (not_173_out, OP5);
  not not_174 (not_174_out, OP4);
  not not_175 (not_175_out, OP3);
  not not_176 (not_176_out, OP2);
  not not_177 (not_177_out, OP1);
  not not_178 (not_178_out, OP0);
  not not_179 (not_179_out, F5);
  not not_180 (not_180_out, F4);
  not not_181 (not_181_out, F3);
  not not_182 (not_182_out, F2);
  not not_183 (not_183_out, F0);
  not not_184 (not_184_out, OP5);
  not not_185 (not_185_out, OP4);
  not not_186 (not_186_out, OP3);
  not not_187 (not_187_out, OP2);
  not not_188 (not_188_out, OP1);
  not not_189 (not_189_out, OP0);
  not not_190 (not_190_out, F4);
  not not_191 (not_191_out, F3);
  not not_192 (not_192_out, F2);
  not not_193 (not_193_out, F1);
  not not_194 (not_194_out, F0);
  not not_195 (not_195_out, OP5);
  not not_196 (not_196_out, OP4);
  not not_197 (not_197_out, OP3);
  not not_198 (not_198_out, OP2);
  not not_199 (not_199_out, OP1);
  not not_200 (not_200_out, OP0);
  not not_201 (not_201_out, F4);
  not not_202 (not_202_out, F3);
  not not_203 (not_203_out, F2);
  not not_204 (not_204_out, F1);
  not not_205 (not_205_out, OP5);
  not not_206 (not_206_out, OP4);
  not not_207 (not_207_out, OP3);
  not not_208 (not_208_out, OP2);
  not not_209 (not_209_out, OP1);
  not not_210 (not_210_out, OP0);
  not not_211 (not_211_out, F4);
  not not_212 (not_212_out, F3);
  not not_213 (not_213_out, F2);
  not not_214 (not_214_out, F0);
  not not_215 (not_215_out, OP5);
  not not_216 (not_216_out, OP4);
  not not_217 (not_217_out, OP3);
  not not_218 (not_218_out, OP2);
  not not_219 (not_219_out, OP1);
  not not_220 (not_220_out, OP0);
  not not_221 (not_221_out, F4);
  not not_222 (not_222_out, F3);
  not not_223 (not_223_out, F1);
  not not_224 (not_224_out, F0);
  not not_225 (not_225_out, OP5);
  not not_226 (not_226_out, OP4);
  not not_227 (not_227_out, OP3);
  not not_228 (not_228_out, OP2);
  not not_229 (not_229_out, OP1);
  not not_230 (not_230_out, OP0);
  not not_231 (not_231_out, F4);
  not not_232 (not_232_out, F3);
  not not_233 (not_233_out, F1);
  not not_234 (not_234_out, OP5);
  not not_235 (not_235_out, OP4);
  not not_236 (not_236_out, OP3);
  not not_237 (not_237_out, OP2);
  not not_238 (not_238_out, OP1);
  not not_239 (not_239_out, OP0);
  not not_240 (not_240_out, F4);
  not not_241 (not_241_out, F3);
  not not_242 (not_242_out, OP5);
  not not_243 (not_243_out, OP4);
  not not_244 (not_244_out, OP3);
  not not_245 (not_245_out, OP2);
  not not_246 (not_246_out, OP1);
  not not_247 (not_247_out, OP0);
  not not_248 (not_248_out, F4);
  not not_249 (not_249_out, F2);
  not not_250 (not_250_out, F0);
  not not_251 (not_251_out, OP5);
  not not_252 (not_252_out, OP4);
  not not_253 (not_253_out, OP3);
  not not_254 (not_254_out, OP2);
  not not_255 (not_255_out, OP1);
  not not_256 (not_256_out, OP0);
  not not_257 (not_257_out, F4);
  not not_258 (not_258_out, F2);
  not not_259 (not_259_out, OP5);
  not not_260 (not_260_out, OP4);
  not not_261 (not_261_out, OP3);
  not not_262 (not_262_out, OP2);
  not not_263 (not_263_out, OP1);
  not not_264 (not_264_out, OP0);
  not not_265 (not_265_out, F5);
  not not_266 (not_266_out, F4);
  not not_267 (not_267_out, F1);
  not not_268 (not_268_out, F0);
  not not_269 (not_269_out, OP5);
  not not_270 (not_270_out, OP4);
  not not_271 (not_271_out, OP3);
  not not_272 (not_272_out, OP1);
  not not_273 (not_273_out, OP0);
  not not_274 (not_274_out, OP5);
  not not_275 (not_275_out, OP4);
  not not_276 (not_276_out, OP3);
  not not_277 (not_277_out, OP1);
  not not_278 (not_278_out, OP4);
  not not_279 (not_279_out, OP2);
  not not_280 (not_280_out, OP5);
  not not_281 (not_281_out, OP4);
  not not_282 (not_282_out, OP3);
  not not_283 (not_283_out, OP2);
  not not_284 (not_284_out, OP1);
  not not_285 (not_285_out, OP0);
  not not_286 (not_286_out, F5);
  not not_287 (not_287_out, F4);
  not not_288 (not_288_out, F3);
  and and_1 (and_1_out, not_1_out, not_2_out, not_3_out, not_4_out, not_5_out, not_6_out, F5, not_7_out, not_8_out, not_9_out, not_10_out, not_11_out);
  and and_2 (and_2_out, not_12_out, not_13_out, not_14_out, not_15_out, not_16_out, not_17_out, F5, not_18_out, not_19_out, not_20_out, not_21_out, F0);
  and and_3 (and_3_out, not_22_out, not_23_out, not_24_out, not_25_out, not_26_out, not_27_out, F5, not_28_out, not_29_out, not_30_out, F1, not_31_out);
  and and_4 (and_4_out, not_32_out, not_33_out, not_34_out, not_35_out, not_36_out, not_37_out, F5, not_38_out, not_39_out, F2, not_40_out, not_41_out);
  and and_5 (and_5_out, not_42_out, not_43_out, not_44_out, not_45_out, not_46_out, not_47_out, F5, not_48_out, not_49_out, F2, not_50_out, F0);
  and and_6 (and_6_out, not_51_out, not_52_out, not_53_out, not_54_out, not_55_out, not_56_out, F5, not_57_out, not_58_out, F2, F1, F0);
  and and_7 (and_7_out, not_59_out, not_60_out, not_61_out, not_62_out, not_63_out, not_64_out, F5, not_65_out, F3, not_66_out, F1, not_67_out);
  and and_8 (and_8_out, not_68_out, not_69_out, not_70_out, not_71_out, not_72_out, not_73_out, F5, not_74_out, F3, not_75_out, F1, F0);
  and and_9 (and_9_out, not_76_out, not_77_out, not_78_out, not_79_out, not_80_out, not_81_out, not_82_out, not_83_out, F3, not_84_out, not_85_out, not_86_out);
  and and_10 (and_10_out, not_87_out, not_88_out, not_89_out, not_90_out, not_91_out, not_92_out, not_93_out, not_94_out, F3, F2, not_95_out, not_96_out);
  and and_11 (and_11_out, not_97_out, not_98_out, not_99_out, OP2, not_100_out, not_101_out);
  and and_12 (and_12_out, not_102_out, not_103_out, not_104_out, OP2, not_105_out, OP0);
  and and_13 (and_13_out, not_106_out, not_107_out, OP3, not_108_out, not_109_out, not_110_out);
  and and_14 (and_14_out, not_111_out, not_112_out, OP3, OP2, not_113_out, not_114_out);
  and and_15 (and_15_out, not_115_out, not_116_out, OP3, not_117_out, not_118_out, OP0);
  and and_16 (and_16_out, not_119_out, not_120_out, OP3, not_121_out, OP1, not_122_out);
  and and_17 (and_17_out, not_123_out, not_124_out, OP3, OP2, not_125_out, OP0);
  and and_18 (and_18_out, OP5, not_126_out, not_127_out, not_128_out, OP1, OP0);
  and and_19 (and_19_out, OP5, not_129_out, OP3, not_130_out, OP1, OP0);
  and and_20 (and_20_out, not_131_out, not_132_out, not_133_out, not_134_out, not_135_out, not_136_out, not_137_out, not_138_out, not_139_out, F2, F1, F0);
  and and_21 (and_21_out, not_140_out, not_141_out, OP3, not_142_out, OP1, OP0);
  and and_22 (and_22_out, OP5, not_143_out, not_144_out, OP2, not_145_out, OP0);
  and and_23 (and_23_out, not_146_out, not_147_out, not_148_out, not_149_out, not_150_out, OP0);
  and and_24 (and_24_out, not_151_out, not_152_out, not_153_out, not_154_out, not_155_out, not_156_out, not_157_out, not_158_out, not_159_out, not_160_out, not_161_out, not_162_out);
  and and_25 (and_25_out, not_163_out, not_164_out, not_165_out, not_166_out, not_167_out, not_168_out, not_169_out, not_170_out, not_171_out, not_172_out, F1, F0);
  and and_26 (and_26_out, not_173_out, not_174_out, not_175_out, not_176_out, not_177_out, not_178_out, not_179_out, not_180_out, not_181_out, not_182_out, F1, not_183_out);
  and and_27 (and_27_out, not_184_out, not_185_out, not_186_out, not_187_out, not_188_out, not_189_out, F5, not_190_out, not_191_out, not_192_out, not_193_out, not_194_out);
  and and_28 (and_28_out, not_195_out, not_196_out, not_197_out, not_198_out, not_199_out, not_200_out, F5, not_201_out, not_202_out, not_203_out, not_204_out, F0);
  and and_29 (and_29_out, not_205_out, not_206_out, not_207_out, not_208_out, not_209_out, not_210_out, F5, not_211_out, not_212_out, not_213_out, F1, not_214_out);
  and and_30 (and_30_out, not_215_out, not_216_out, not_217_out, not_218_out, not_219_out, not_220_out, F5, not_221_out, not_222_out, F2, not_223_out, not_224_out);
  and and_31 (and_31_out, not_225_out, not_226_out, not_227_out, not_228_out, not_229_out, not_230_out, F5, not_231_out, not_232_out, F2, not_233_out, F0);
  and and_32 (and_32_out, not_234_out, not_235_out, not_236_out, not_237_out, not_238_out, not_239_out, F5, not_240_out, not_241_out, F2, F1, F0);
  and and_33 (and_33_out, not_242_out, not_243_out, not_244_out, not_245_out, not_246_out, not_247_out, F5, not_248_out, F3, not_249_out, F1, not_250_out);
  and and_34 (and_34_out, not_251_out, not_252_out, not_253_out, not_254_out, not_255_out, not_256_out, F5, not_257_out, F3, not_258_out, F1, F0);
  and and_35 (and_35_out, not_259_out, not_260_out, not_261_out, not_262_out, not_263_out, not_264_out, not_265_out, not_266_out, F3, F2, not_267_out, not_268_out);
  and and_36 (and_36_out, not_269_out, not_270_out, not_271_out, OP2, not_272_out, not_273_out);
  and and_37 (and_37_out, not_274_out, not_275_out, not_276_out, OP2, not_277_out, OP0);
  and and_38 (and_38_out, OP5, not_278_out, OP3, not_279_out, OP1, OP0);
  and and_39 (and_39_out, not_280_out, not_281_out, not_282_out, not_283_out, not_284_out, not_285_out, not_286_out, not_287_out, not_288_out, F2, F1, F0);
  or or_1 (R1_Used, and_1_out, and_2_out, and_3_out, and_4_out, and_5_out, and_6_out, and_7_out, and_8_out, and_9_out, and_10_out, and_11_out, and_12_out, and_13_out, and_14_out, and_15_out, and_16_out, and_17_out, and_18_out, and_19_out, and_20_out, and_21_out, and_22_out, and_23_out);
  or or_2 (R2_Used, and_24_out, and_25_out, and_26_out, and_27_out, and_28_out, and_29_out, and_30_out, and_31_out, and_32_out, and_33_out, and_34_out, and_35_out, and_36_out, and_37_out, and_38_out, and_39_out);
endmodule

module \数据相关检测  (
  input  [5:0] OP,
  input  [4:0] EX_WriteReg_num,
  input  EX_RegWrite,
  input  [4:0] MEM_WriteReg_num,
  input  MEM_RegWrite,
  input  [5:0] Func,
  input  [4:0] ID_R1_num,
  input  [4:0] ID_R2_num,
  output \数据相关 ,
  output [1:0] foward_A,
  output [1:0] forward_B
);

  wire and_5_out, and_6_out, and_7_out, and_8_out, comparator_1_eq, comparator_2_eq, comparator_3_eq,
       comparator_4_eq, comparator_5_eq, comparator_6_eq, or_1_out, or_2_out, R1_Used, R2_Used;
  wire [1:0] and_2_out, and_4_out;

  \源寄存器使用情况  \u_源寄存器使用情况_1  (
    .OP0(OP[0]), .OP1(OP[1]), .OP2(OP[2]), .OP3(OP[3]), .OP4(OP[4]), .OP5(OP[5]), .F0(Func[0]), .F1(Func[1]),
    .F2(Func[2]), .F3(Func[3]), .F4(Func[4]), .F5(Func[5]), .R1_Used(R1_Used), .R2_Used(R2_Used));
  Comparator #(.width(5)) comparator_1 (.a(ID_R1_num), .b(EX_WriteReg_num), .eq(comparator_1_eq));  // open: gt, lt
  Comparator #(.width(5)) comparator_2 (.a(ID_R1_num), .b(MEM_WriteReg_num), .eq(comparator_2_eq));  // open: gt, lt
  Comparator #(.width(5)) comparator_3 (.a(ID_R2_num), .b(EX_WriteReg_num), .eq(comparator_3_eq));  // open: gt, lt
  Comparator #(.width(5)) comparator_4 (.a(ID_R2_num), .b(MEM_WriteReg_num), .eq(comparator_4_eq));  // open: gt, lt
  and and_1 (and_2_out[1], comparator_1_eq, EX_RegWrite);
  and and_2 (and_2_out[0], comparator_2_eq, MEM_RegWrite);
  and and_3 (and_4_out[1], comparator_3_eq, EX_RegWrite);
  and and_4 (and_4_out[0], comparator_4_eq, MEM_RegWrite);
  Comparator #(.width(5)) comparator_5 (.a(ID_R1_num), .b({5{1'b0}}), .eq(comparator_5_eq));  // open: gt, lt
  or or_1 (or_1_out, and_2_out[1], and_2_out[0]);
  Comparator #(.width(5)) comparator_6 (.a(ID_R2_num), .b({5{1'b0}}), .eq(comparator_6_eq));  // open: gt, lt
  or or_2 (or_2_out, and_4_out[1], and_4_out[0]);
  and and_5 (and_5_out, or_1_out, R1_Used);
  and and_6 (and_6_out, or_2_out, R2_Used);
  and and_7 (and_7_out, ~comparator_5_eq, and_5_out);  // AND_Gate
  and and_8 (and_8_out, ~comparator_6_eq, and_6_out);  // AND_Gate
  Multiplexer #(.width(2), .enable("false")) multiplexer_1 (
    .in0(2'b00), .in1(and_2_out), .out(foward_A), .sel(and_7_out));
  or or_3 (\数据相关 , and_7_out, and_8_out);
  Multiplexer #(.width(2), .enable("false")) multiplexer_2 (
    .in0(2'b00), .in1(and_4_out), .out(forward_B), .sel(and_8_out));

  // Other names for the same wires on the sheet: OP_CODE[5:0] = OP

  // Notes on the sheet:
  //   说明当前指令所需要的数据准备要写回寄存器,可从Din获得
  //   说明当前指令所需要AluResult的数据，可从Mem.Alu_result获得
  //   说明当前指令所需要的数据准备要写回寄存器,可从Din获得
  //   说明当前指令所需要AluResult的数据，可从Mem.Alu_result获得
endmodule

module IF_ID (
  input  [31:0] PC_in,
  input  [31:0] Instruction_in,
  input  CLK,
  input  \同步清零端_高电平有效 ,
  input  \使能端_低电平有效 ,
  input  Reset,
  output [31:0] PC_out,
  output [31:0] Instruction_out
);

  wire not_1_out;
  wire [31:0] multiplexer_1_out, multiplexer_2_out;

  Multiplexer #(.width(32), .enable("false")) multiplexer_1 (
    .in0(PC_in), .in1({32{1'b0}}), .out(multiplexer_1_out), .sel(\同步清零端_高电平有效 ));
  Multiplexer #(.width(32), .enable("false")) multiplexer_2 (
    .in0(Instruction_in), .in1({32{1'b0}}), .out(multiplexer_2_out), .sel(\同步清零端_高电平有效 ));
  not not_1 (not_1_out, \使能端_低电平有效 );
  Register #(.width(32)) register_1 (.D(multiplexer_1_out), .en(not_1_out), .Q(PC_out), .clk(CLK), .clr(Reset));
  Register #(.width(32)) register_2 (
    .D(multiplexer_2_out), .en(not_1_out), .Q(Instruction_out), .clk(CLK), .clr(Reset));

  // Notes on the sheet:
  //   使能端_低电平有效: pull=down
  //   同步清零端_高电平有效: pull=down
endmodule

module ID_EX (
  input  [5:0] WB,
  input  MemWrite,
  input  [10:0] EX,
  input  [31:0] PC_in,
  input  [31:0] Instruction_in,
  input  [31:0] RD1,
  input  [31:0] RD2,
  input  [31:0] imm_in,
  input  [4:0] shmat,
  input  [4:0] W_num,
  input  [1:0] forward_A,
  input  [1:0] forward_B,
  input  Load_Use,
  input  CLK,
  input  \同步清零端_高电平有效 ,
  input  \使能端_低电平有效 ,
  input  Reset,
  output [5:0] WB_2,
  output MemWrite_2,
  output [10:0] EX_2,
  output [31:0] PC_out,
  output [31:0] Instruction_out,
  output [31:0] A,
  output [31:0] B,
  output [31:0] imm_out,
  output [4:0] shmat_2,
  output [4:0] W_num_2,
  output [1:0] forward_A_2,
  output [1:0] forward_B_2,
  output Load_use_2
);

  wire multiplexer_2_out, multiplexer_13_out, not_1_out;
  wire [1:0] multiplexer_11_out, multiplexer_12_out;
  wire [4:0] multiplexer_9_out, multiplexer_10_out;
  wire [5:0] multiplexer_1_out;
  wire [10:0] multiplexer_3_out;
  wire [31:0] multiplexer_4_out, multiplexer_5_out, multiplexer_6_out, multiplexer_7_out, multiplexer_8_out;

  Multiplexer #(.width(6), .enable("false")) multiplexer_1 (
    .in0(WB), .in1({6{1'b0}}), .out(multiplexer_1_out), .sel(\同步清零端_高电平有效 ));
  Multiplexer #(.enable("false")) multiplexer_2 (
    .in0(MemWrite), .in1(1'b0), .out(multiplexer_2_out), .sel(\同步清零端_高电平有效 ));
  Multiplexer #(.width(11), .enable("false")) multiplexer_3 (
    .in0(EX), .in1({11{1'b0}}), .out(multiplexer_3_out), .sel(\同步清零端_高电平有效 ));
  Multiplexer #(.width(32), .enable("false")) multiplexer_4 (
    .in0(PC_in), .in1({32{1'b0}}), .out(multiplexer_4_out), .sel(\同步清零端_高电平有效 ));
  Multiplexer #(.width(32), .enable("false")) multiplexer_5 (
    .in0(Instruction_in), .in1({32{1'b0}}), .out(multiplexer_5_out), .sel(\同步清零端_高电平有效 ));
  Multiplexer #(.width(32), .enable("false")) multiplexer_6 (
    .in0(RD1), .in1({32{1'b0}}), .out(multiplexer_6_out), .sel(\同步清零端_高电平有效 ));
  Multiplexer #(.width(32), .enable("false")) multiplexer_7 (
    .in0(RD2), .in1({32{1'b0}}), .out(multiplexer_7_out), .sel(\同步清零端_高电平有效 ));
  Multiplexer #(.width(32), .enable("false")) multiplexer_8 (
    .in0(imm_in), .in1({32{1'b0}}), .out(multiplexer_8_out), .sel(\同步清零端_高电平有效 ));
  Multiplexer #(.width(5), .enable("false")) multiplexer_9 (
    .in0(shmat), .in1({5{1'b0}}), .out(multiplexer_9_out), .sel(\同步清零端_高电平有效 ));
  Multiplexer #(.width(5), .enable("false")) multiplexer_10 (
    .in0(W_num), .in1({5{1'b0}}), .out(multiplexer_10_out), .sel(\同步清零端_高电平有效 ));
  Multiplexer #(.width(2), .enable("false")) multiplexer_11 (
    .in0(forward_A), .in1(2'b00), .out(multiplexer_11_out), .sel(\同步清零端_高电平有效 ));
  Multiplexer #(.width(2), .enable("false")) multiplexer_12 (
    .in0(forward_B), .in1(2'b00), .out(multiplexer_12_out), .sel(\同步清零端_高电平有效 ));
  Multiplexer #(.enable("false")) multiplexer_13 (
    .in0(Load_Use), .in1(1'b0), .out(multiplexer_13_out), .sel(\同步清零端_高电平有效 ));
  not not_1 (not_1_out, \使能端_低电平有效 );
  Register #(.width(6)) register_1 (.D(multiplexer_1_out), .en(not_1_out), .Q(WB_2), .clk(CLK), .clr(Reset));
  Register #(.width(1)) register_2 (.D(multiplexer_2_out), .Q(MemWrite_2), .clk(CLK), .clr(Reset));  // open: en
  Register #(.width(11)) register_3 (.D(multiplexer_3_out), .en(not_1_out), .Q(EX_2), .clk(CLK), .clr(Reset));
  Register #(.width(32)) register_4 (.D(multiplexer_4_out), .en(not_1_out), .Q(PC_out), .clk(CLK), .clr(Reset));
  Register #(.width(32)) register_5 (
    .D(multiplexer_5_out), .en(not_1_out), .Q(Instruction_out), .clk(CLK), .clr(Reset));
  Register #(.width(32)) register_6 (.D(multiplexer_6_out), .en(not_1_out), .Q(A), .clk(CLK), .clr(Reset));
  Register #(.width(32)) register_7 (.D(multiplexer_7_out), .en(not_1_out), .Q(B), .clk(CLK), .clr(Reset));
  Register #(.width(32)) register_8 (.D(multiplexer_8_out), .en(not_1_out), .Q(imm_out), .clk(CLK), .clr(Reset));
  Register #(.width(5)) register_9 (.D(multiplexer_9_out), .en(not_1_out), .Q(shmat_2), .clk(CLK), .clr(Reset));
  Register #(.width(5)) register_10 (.D(multiplexer_10_out), .en(not_1_out), .Q(W_num_2), .clk(CLK), .clr(Reset));
  Register #(.width(2)) register_11 (.D(multiplexer_11_out), .en(not_1_out), .Q(forward_A_2), .clk(CLK), .clr(Reset));
  Register #(.width(2)) register_12 (.D(multiplexer_12_out), .en(not_1_out), .Q(forward_B_2), .clk(CLK), .clr(Reset));
  Register #(.width(1)) register_13 (.D(multiplexer_13_out), .en(not_1_out), .Q(Load_use_2), .clk(CLK), .clr(Reset));

  // Notes on the sheet:
  //   使能端_低电平有效: pull=down
  //   同步清零端_高电平有效: pull=down
endmodule
module EX_MEM (
  input  [5:0] WB,
  input  MemWrite,
  input  [31:0] PC_in,
  input  [31:0] Instruction_in,
  input  [31:0] B,
  input  [31:0] Alu_result,
  input  [4:0] W_num,
  input  [31:0] A,
  input  CLK,
  input  \同步清零端_高电平有效 ,
  input  \使能端_低电平有效 ,
  input  Reset,
  output [5:0] WB_2,
  output MemWrite_2,
  output [31:0] PC_out,
  output [31:0] Instruction_out,
  output [31:0] B_2,
  output [31:0] Alu_result_2,
  output [4:0] W_num_2,
  output [31:0] A_2
);

  wire multiplexer_2_out, not_1_out;
  wire [4:0] multiplexer_7_out;
  wire [5:0] multiplexer_1_out;
  wire [31:0] multiplexer_3_out, multiplexer_4_out, multiplexer_5_out, multiplexer_6_out, multiplexer_8_out;

  Multiplexer #(.width(6), .enable("false")) multiplexer_1 (
    .in0(WB), .in1({6{1'b0}}), .out(multiplexer_1_out), .sel(\同步清零端_高电平有效 ));
  Multiplexer #(.enable("false")) multiplexer_2 (
    .in0(MemWrite), .in1(1'b0), .out(multiplexer_2_out), .sel(\同步清零端_高电平有效 ));
  Multiplexer #(.width(32), .enable("false")) multiplexer_3 (
    .in0(PC_in), .in1({32{1'b0}}), .out(multiplexer_3_out), .sel(\同步清零端_高电平有效 ));
  Multiplexer #(.width(32), .enable("false")) multiplexer_4 (
    .in0(Instruction_in), .in1({32{1'b0}}), .out(multiplexer_4_out), .sel(\同步清零端_高电平有效 ));
  Multiplexer #(.width(32), .enable("false")) multiplexer_5 (
    .in0(B), .in1({32{1'b0}}), .out(multiplexer_5_out), .sel(\同步清零端_高电平有效 ));
  Multiplexer #(.width(32), .enable("false")) multiplexer_6 (
    .in0(Alu_result), .in1({32{1'b0}}), .out(multiplexer_6_out), .sel(\同步清零端_高电平有效 ));
  Multiplexer #(.width(5), .enable("false")) multiplexer_7 (
    .in0(W_num), .in1({5{1'b0}}), .out(multiplexer_7_out), .sel(\同步清零端_高电平有效 ));
  Multiplexer #(.width(32), .enable("false")) multiplexer_8 (
    .in0(A), .in1({32{1'b0}}), .out(multiplexer_8_out), .sel(\同步清零端_高电平有效 ));
  not not_1 (not_1_out, \使能端_低电平有效 );
  Register #(.width(6)) register_1 (.D(multiplexer_1_out), .en(not_1_out), .Q(WB_2), .clk(CLK), .clr(Reset));
  Register #(.width(1)) register_2 (.D(multiplexer_2_out), .en(not_1_out), .Q(MemWrite_2), .clk(CLK), .clr(Reset));
  Register #(.width(32)) register_3 (.D(multiplexer_3_out), .en(not_1_out), .Q(PC_out), .clk(CLK), .clr(Reset));
  Register #(.width(32)) register_4 (
    .D(multiplexer_4_out), .en(not_1_out), .Q(Instruction_out), .clk(CLK), .clr(Reset));
  Register #(.width(32)) register_5 (.D(multiplexer_5_out), .en(not_1_out), .Q(B_2), .clk(CLK), .clr(Reset));
  Register #(.width(32)) register_6 (.D(multiplexer_6_out), .en(not_1_out), .Q(Alu_result_2), .clk(CLK), .clr(Reset));
  Register #(.width(5)) register_7 (.D(multiplexer_7_out), .en(not_1_out), .Q(W_num_2), .clk(CLK), .clr(Reset));
  Register #(.width(32)) register_8 (.D(multiplexer_8_out), .en(not_1_out), .Q(A_2), .clk(CLK), .clr(Reset));

  // Notes on the sheet:
  //   使能端_低电平有效: pull=down
  //   同步清零端_高电平有效: pull=down
endmodule

module MEM_WB (
  input  [5:0] WB,
  input  [31:0] PC_in,
  input  [31:0] Instruction_in,
  input  [31:0] Alu_result,
  input  [31:0] MemData,
  input  [4:0] W_num,
  input  [31:0] A,
  input  [31:0] B,
  input  CLK,
  input  \同步清零端_高电平有效 ,
  input  \使能端_低电平有效 ,
  input  Reset,
  output [5:0] WB_2,
  output [31:0] PC_out,
  output [31:0] Instruction_out,
  output [31:0] Alu_result_2,
  output [31:0] MemData_2,
  output [4:0] W_num_2,
  output [31:0] A_2,
  output [31:0] B_2
);

  wire not_1_out;
  wire [4:0] multiplexer_6_out;
  wire [5:0] multiplexer_1_out;
  wire [31:0] multiplexer_2_out, multiplexer_3_out, multiplexer_4_out, multiplexer_5_out, multiplexer_7_out,
       multiplexer_8_out;

  Multiplexer #(.width(6), .enable("false")) multiplexer_1 (
    .in0(WB), .in1({6{1'b0}}), .out(multiplexer_1_out), .sel(\同步清零端_高电平有效 ));
  Multiplexer #(.width(32), .enable("false")) multiplexer_2 (
    .in0(PC_in), .in1({32{1'b0}}), .out(multiplexer_2_out), .sel(\同步清零端_高电平有效 ));
  Multiplexer #(.width(32), .enable("false")) multiplexer_3 (
    .in0(Instruction_in), .in1({32{1'b0}}), .out(multiplexer_3_out), .sel(\同步清零端_高电平有效 ));
  Multiplexer #(.width(32), .enable("false")) multiplexer_4 (
    .in0(Alu_result), .in1({32{1'b0}}), .out(multiplexer_4_out), .sel(\同步清零端_高电平有效 ));
  Multiplexer #(.width(32), .enable("false")) multiplexer_5 (
    .in0(MemData), .in1({32{1'b0}}), .out(multiplexer_5_out), .sel(\同步清零端_高电平有效 ));
  Multiplexer #(.width(5), .enable("false")) multiplexer_6 (
    .in0(W_num), .in1({5{1'b0}}), .out(multiplexer_6_out), .sel(\同步清零端_高电平有效 ));
  Multiplexer #(.width(32), .enable("false")) multiplexer_7 (
    .in0(A), .in1({32{1'b0}}), .out(multiplexer_7_out), .sel(\同步清零端_高电平有效 ));
  Multiplexer #(.width(32), .enable("false")) multiplexer_8 (
    .in0(B), .in1({32{1'b0}}), .out(multiplexer_8_out), .sel(\同步清零端_高电平有效 ));
  Register #(.width(6)) register_1 (.D(multiplexer_1_out), .en(not_1_out), .Q(WB_2), .clk(CLK), .clr(Reset));
  Register #(.width(32)) register_2 (.D(multiplexer_2_out), .en(not_1_out), .Q(PC_out), .clk(CLK), .clr(Reset));
  Register #(.width(32)) register_3 (
    .D(multiplexer_3_out), .en(not_1_out), .Q(Instruction_out), .clk(CLK), .clr(Reset));
  Register #(.width(32)) register_4 (.D(multiplexer_4_out), .en(not_1_out), .Q(Alu_result_2), .clk(CLK), .clr(Reset));
  Register #(.width(32)) register_5 (.D(multiplexer_5_out), .en(not_1_out), .Q(MemData_2), .clk(CLK), .clr(Reset));
  Register #(.width(5)) register_6 (.D(multiplexer_6_out), .en(not_1_out), .Q(W_num_2), .clk(CLK), .clr(Reset));
  Register #(.width(32)) register_7 (.D(multiplexer_7_out), .en(not_1_out), .Q(A_2), .clk(CLK), .clr(Reset));
  Register #(.width(32)) register_8 (.D(multiplexer_8_out), .en(not_1_out), .Q(B_2), .clk(CLK), .clr(Reset));
  not not_1 (not_1_out, \使能端_低电平有效 );

  // Notes on the sheet:
  //   使能端_低电平有效: pull=down
  //   同步清零端_高电平有效: pull=down
endmodule

module \分支相关流水线  (
);

  wire Alu_srcB, and_1_out, and_2_out, and_3_out, and_4_out, and_5_out, Beq, BGEZ, Bne, Branch, CLK,
       comparator_1_eq, EX_MEM_memwrite_2, Go, ID_EX_p12, ID_EX_p17, IR1, IR2, IR3, JAL, JMP_out, JR_out,
       LHU, MemToReg, MemWrite, mips_alu_1_equal, not_1_out, or_1_out, RegDst, RegWrite, RST, SignedExt,
       SLTIU, Syscall, W1, W2, W3, WB_JAL, WB_LHU, WB_RegWrite, WB_SLTIU, WB_Syscall, \暂停 , \清零 ;
  wire [1:1] MEM_WB_wb_2;
  wire [3:0] Alu_op;
  wire [4:0] EX_MEM_w_num_2, ID_EX_p24, ID_EX_p25, MEM_WB_w_num_2, multiplexer_2_out, multiplexer_3_out,
       multiplexer_4_out, multiplexer_6_out, multiplexer_9_out;
  wire [5:0] EX_MEM_wb_2, ID_EX_p16;
  wire [10:0] ID_EX_p18;
  wire [10:8] EX;
  wire [15:0] \LoadUse次数 , \总周期数 , \插入气泡数 , \无条件分支数 , \条件分支成功数 ;
  wire [31:0] bit_extender_1_out, bit_extender_2_out, Din, EX_ALU_Result, EX_IR, EX_MEM_alu_result_2,
       EX_MEM_b_2, EX_MEM_instruction_out, EX_PC, ID_EX_p21, ID_EX_p22, ID_EX_p23, ID_IR, ID_PC, ID_R1,
       ID_R2, IF_PC, LedData, MEM_PC, MEM_WB_memdata_2, multiplexer_1_out, multiplexer_5_out,
       multiplexer_7_out, multiplexer_8_out, multiplexer_11_out, multiplexer_12_out, multiplexer_13_out,
       PC_q, ram_1_data, rom_1_data, shifter_1_out, WB_ALU_Result, WB_PC, \无条件跳转地址 , \条件分支跳转地址 ;

  Button \u_总复位  (.out(RST));
  Button _1 (.out(IR1));
  Button _2 (.out(IR2));
  Button _3 (.out(IR3));
  Button \u_继续运行  (.out(Go));
  LED led_1 (.in(W1));
  LED led_2 (.in(W2));
  LED led_3 (.in(W3));
  Hex_Digit_Display hex_digit_display_1 (.value(LedData[31:28]));  // open: dp
  Comparator #(.width(32)) comparator_1 (.a(ID_R1), .b(32'h22), .eq(comparator_1_eq));  // open: gt, lt
  Hex_Digit_Display hex_digit_display_2 (.value(LedData[23:20]));  // open: dp
  Hex_Digit_Display hex_digit_display_3 (.value(LedData[27:24]));  // open: dp
  Multiplexer #(.select(2), .width(32), .enable("false")) multiplexer_1 (
    .in0(IF_PC), .in1(\无条件跳转地址 ), .in2(\条件分支跳转地址 ), .in3({32{1'b0}}), .out(multiplexer_1_out),
    .sel({Branch, JMP_out}));
  and and_1 (and_1_out, comparator_1_eq, WB_Syscall);
  and and_2 (and_2_out, ~comparator_1_eq, WB_Syscall);  // AND_Gate
  Hex_Digit_Display hex_digit_display_4 (.value(LedData[19:16]));  // open: dp
  Hex_Digit_Display hex_digit_display_5 (.value(LedData[15:12]));  // open: dp
  Adder #(.width(32)) adder_1 (.a(32'h4), .b(PC_q), .out(IF_PC));  // open: cin, cout
  Register #(.width(32)) PC (.D(multiplexer_1_out), .en(\暂停 ), .Q(PC_q), .clk(CLK), .clr(RST));
  Register #(.width(32)) register_1 (.D(ID_R2), .en(and_1_out), .Q(LedData), .clk(CLK), .clr(RST));
  D_Flip_Flop d_ff_1 (.clk(CLK), .D(and_2_out), .Qn(\暂停 ), .preset(1'b0), .en(\暂停 ), .reset(or_1_out));  // open: Q
  or or_1 (or_1_out, RST, Go);
  Hex_Digit_Display hex_digit_display_6 (.value(LedData[11:8]));  // open: dp
  Hex_Digit_Display hex_digit_display_7 (.value(LedData[7:4]));  // open: dp
  Clock clock_1 (.out(CLK));
  Hex_Digit_Display hex_digit_display_8 (.value(LedData[3:0]));  // open: dp
  ROM #(.addrWidth(10), .dataWidth(32)) rom_1 (.addr(PC_q[11:2]), .data(rom_1_data));  // open: sel
  IF_ID IF_ID (
    .PC_in(IF_PC), .Instruction_in(rom_1_data), .PC_out(ID_PC), .Instruction_out(ID_IR),
    .\同步清零端_高电平有效 (\清零 ), .CLK(CLK), .Reset(RST));  // open: 使能端_低电平有效
  Counter #(.width(16), .max('hffff)) counter_1 (
    .count(\暂停 ), .Q(\总周期数 ), .clk(CLK), .clr(RST));  // open: load, D, carry
  // Probe on \总周期数 
  // Probe on \无条件分支数 
  // Probe on \条件分支成功数 
  // Probe on \插入气泡数 
  // Probe on \LoadUse次数 
  // Probe on IF_PC[11:0]
  Multiplexer #(.width(5), .enable("false")) multiplexer_2 (
    .in0(ID_IR[25:21]), .in1(5'b00010), .out(multiplexer_2_out), .sel(WB_Syscall));
  Multiplexer #(.width(5), .enable("false")) multiplexer_3 (
    .in0(ID_IR[20:16]), .in1(5'b00100), .out(multiplexer_3_out), .sel(WB_Syscall));
  assign bit_extender_1_out = {{16{1'b0}}, ID_IR[15:0]};  // Bit_Extender bit_extender_1
  assign bit_extender_2_out = {{16{ID_IR[15]}}, ID_IR[15:0]};  // Bit_Extender bit_extender_2
  // Probe on ID_PC[11:0]
  Multiplexer #(.width(5), .enable("false")) multiplexer_4 (
    .in0(ID_IR[20:16]), .in1(ID_IR[15:11]), .out(multiplexer_4_out), .sel(RegDst));
  Multiplexer #(.width(32), .enable("false")) multiplexer_5 (
    .in0(bit_extender_1_out), .in1(bit_extender_2_out), .out(multiplexer_5_out), .sel(SignedExt));
  // Probe on MEM_PC[11:0]
  // Probe on EX_PC[11:0]
  \硬布线控制器  \u_硬布线控制器_1  (
    .Func(ID_IR[5:0]), .OP(ID_IR[31:26]), .ALU_OP(Alu_op), .MemToReg(MemToReg), .MemWrite(MemWrite),
    .ALU_SRC(Alu_srcB), .RegWrite(RegWrite), .SysCALL(Syscall), .SignedExt(SignedExt), .RegDst(RegDst),
    .JR(EX[8]), .JMP(EX[9]), .Beq(Beq), .JAL(JAL), .Bne(Bne), .LHU(LHU), .BGEZ(BGEZ), .SLTIU(SLTIU),
    .SRAV(EX[10]));
  // Probe on WB_PC[11:0]
  Multiplexer #(.width(5), .enable("false")) multiplexer_6 (
    .in0(MEM_WB_w_num_2), .in1({5{1'b1}}), .out(multiplexer_6_out), .sel(WB_JAL));
  MIPS_Regifile mips_regifile_1 (
    .Din(Din), .Clk(CLK), .R1(ID_R1), .R2(ID_R2), .WE(WB_RegWrite), .W_num(multiplexer_6_out),
    .R1_num(multiplexer_2_out), .R2_num(multiplexer_3_out));
  or or_2 (\清零 , Branch, JMP_out);
  // ID_EX ID_EX: pin names not known; wires that end beside it: {LHU, SLTIU, JAL, Syscall, MemToReg, RegWrite}, MemWrite, {EX, BGEZ, Bne, Beq, Alu_srcB, Alu_op}, ID_PC, ID_IR, ID_R1, ID_R2, multiplexer_5_out, ID_IR[10:6], multiplexer_4_out, \清零 , ID_EX_p12, ID_EX_p12, CLK, RST, ID_EX_p16, ID_EX_p17, {ID_EX_p18[10], JMP_out, JR_out, ID_EX_p18[7:0]}, EX_PC, EX_IR, ID_EX_p21, ID_EX_p22, ID_EX_p23, ID_EX_p24, ID_EX_p25
  Multiplexer #(.width(32), .enable("false")) multiplexer_7 (
    .in0(ID_EX_p22), .in1({32{1'b0}}), .out(multiplexer_7_out), .sel(ID_EX_p18[7]));
  Multiplexer #(.width(32), .enable("false")) multiplexer_8 (
    .in0(multiplexer_7_out), .in1(ID_EX_p23), .out(multiplexer_8_out), .sel(ID_EX_p18[4]));
  Shifter #(.width(32)) shifter_1 (.in(ID_EX_p23), .\dist (5'b00010), .out(shifter_1_out));
  and and_3 (and_3_out, ID_EX_p18[7], ~EX_ALU_Result[0]);  // AND_Gate
  and and_4 (and_4_out, ID_EX_p18[5], mips_alu_1_equal);
  and and_5 (and_5_out, ID_EX_p18[6], ~mips_alu_1_equal);  // AND_Gate
  MIPS_ALU mips_alu_1 (
    .X(ID_EX_p21), .Y(multiplexer_8_out), .AluOP(ID_EX_p18[3:0]), .Equal(mips_alu_1_equal),
    .Result(EX_ALU_Result), .shamt(multiplexer_9_out));  // open: Result_2
  Multiplexer #(.width(5), .enable("false")) multiplexer_9 (
    .in0(ID_EX_p24), .in1(ID_EX_p21[4:0]), .out(multiplexer_9_out), .sel(ID_EX_p18[10]));
  Adder #(.width(32)) adder_2 (.a(shifter_1_out), .b(EX_PC), .out(\条件分支跳转地址 ));  // open: cin, cout
  Multiplexer #(.width(32), .enable("false")) multiplexer_10 (
    .in0({EX_PC[31:28], EX_IR[25:0], 2'b00}), .in1(ID_EX_p21), .out(\无条件跳转地址 ), .sel(JR_out));
  or or_3 (Branch, and_4_out, and_3_out, and_5_out);
  EX_MEM EX_MEM (
    .MemWrite(ID_EX_p17), .PC_in(EX_PC), .Instruction_in(EX_IR), .B(ID_EX_p22), .Alu_result(EX_ALU_Result),
    .MemWrite_2(EX_MEM_memwrite_2), .PC_out(MEM_PC), .Instruction_out(EX_MEM_instruction_out),
    .B_2(EX_MEM_b_2), .Alu_result_2(EX_MEM_alu_result_2), .CLK(CLK), .W_num(ID_EX_p25),
    .W_num_2(EX_MEM_w_num_2), .WB(ID_EX_p16), .WB_2(EX_MEM_wb_2), .Reset(RST));  // open: 同步清零端_高电平有效, 使能端_低电平有效, A, A_2
  RAM #(.addrWidth(10), .dataWidth(32), .bus("separate")) ram_1 (
    .addr(EX_MEM_alu_result_2[11:2]), .din(EX_MEM_b_2), .data(ram_1_data), .str(EX_MEM_memwrite_2),
    .clk(CLK), .ld(not_1_out), .clr(RST));  // open: sel
  not not_1 (not_1_out, EX_MEM_memwrite_2);
  MEM_WB MEM_WB (
    .PC_in(MEM_PC), .Instruction_in(EX_MEM_instruction_out), .Alu_result(EX_MEM_alu_result_2),
    .MemData(ram_1_data), .PC_out(WB_PC), .Alu_result_2(WB_ALU_Result), .MemData_2(MEM_WB_memdata_2),
    .CLK(CLK), .W_num(EX_MEM_w_num_2), .W_num_2(MEM_WB_w_num_2), .WB(EX_MEM_wb_2),
    .WB_2({WB_LHU, WB_SLTIU, WB_JAL, WB_Syscall, MEM_WB_wb_2[1], WB_RegWrite}), .Reset(RST));  // open: Instruction_out, 同步清零端_高电平有效, 使能端_低电平有效, A, A_2, B, B_2
  Multiplexer #(.width(32), .enable("false")) multiplexer_11 (
    .in0(WB_ALU_Result), .in1(MEM_WB_memdata_2), .out(multiplexer_11_out), .sel(MEM_WB_wb_2[1]));
  Multiplexer #(.width(32), .enable("false")) multiplexer_12 (
    .in0(multiplexer_11_out), .in1(WB_PC), .out(multiplexer_12_out), .sel(WB_JAL));
  Multiplexer #(.width(32), .enable("false")) multiplexer_13 (
    .in0({{16{1'b0}}, multiplexer_11_out[15:0]}), .in1({{16{1'b0}}, multiplexer_11_out[31:16]}),
    .out(multiplexer_13_out), .sel(WB_ALU_Result[1]));
  Multiplexer #(.select(2), .width(32), .enable("false")) multiplexer_14 (
    .in0(multiplexer_12_out), .in1(WB_ALU_Result), .in2(multiplexer_13_out), .in3({32{1'b0}}), .out(Din),
    .sel({WB_LHU, WB_SLTIU}));

  // Other names for the same wires on the sheet: EX[7:0] = {BGEZ, Bne, Beq, Alu_srcB, Alu_op}; JR = EX[8];
  //   JMP = EX[9]; SRAV = EX[10]; PCSel[1:0] = {Branch, JMP_out};
  //   WB[5:0] = {LHU, SLTIU, JAL, Syscall, MemToReg, RegWrite}

  // Notes on the sheet:
  //   中断源
  //   中断等待指示
  //   数码管输出
  //   指令存储器
  //   contents of rom_1 (hex, n*v repeats v):
  //   20110004 ae310000 8e320000 2252fffc 20100000 22110001 2118020 22520004 ae500000 22310001 2118020
  //   22520004 ae500000 22310001 2118020 22520004 ae500000 22310001 2118020 22520004 ae500000 22310001
  //   2118020 22520004 ae500000 22310001 2118020 22520004 ae500000 22310001 2118020 22520004 ae500000
  //   2002000a 20100000 20100000 20100000 c
  //   指令字
  //   OP
  //   rs
  //   rt
  //   rd
  //   imm
  //   OP
  //   Func
  //   流水调试日志用
  //   Alu_op
  //   Alu_src
  //   Beq
  //   Bne
  //   BGEZ
  //   JR
  //   JMP
  //   SRAV
  //   MemToReg
  //   半字片选
endmodule

module \气泡流水线  (
);

  wire Alu_srcB, and_1_out, and_2_out, and_3_out, and_5_out, and_6_out, and_7_out, and_8_out, and_9_out,
       and_10_out, Beq, BGEZ, Bne, Branch, CLK, comparator_1_eq, EN, EX_MEM_memwrite_2, EX_RegWrite, Go,
       Halt, ID_EX_p12, ID_EX_p17, IR1, IR2, IR3, JAL, JMP_out, JR_out, LHU, MEM_RegWrite, MemToReg,
       MemWrite, mips_alu_1_equal, not_2_out, or_1_out, or_3_out, RegDst, RegWrite, RST, SignedExt, SLTIU,
       Syscall, W1, W2, W3, WB_JAL, WB_LHU, WB_RegWrite, WB_SLTIU, \数据相关 , \暂停 , \清零 ;
  wire [2:1] MEM_WB_wb_2;
  wire [3:0] Alu_op;
  wire [4:0] EX_WriteReg_num, ID_EX_p24, ID_R1_num, ID_R2_num, MEM_WB_w_num_2, MEM_WriteReg_num,
       multiplexer_4_out, multiplexer_6_out, multiplexer_9_out;
  wire [5:1] EX_MEM_wb_2, ID_EX_p16;
  wire [10:0] ID_EX_p18;
  wire [10:8] EX;
  wire [15:0] \LoadUse次数 , \总周期数 , \插入气泡数 , \无条件分支数 , \条件分支成功数 ;
  wire [31:0] bit_extender_1_out, bit_extender_2_out, Din, EX_ALU_Result, EX_IR, EX_MEM_alu_result_2,
       EX_MEM_b_2, EX_MEM_instruction_out, EX_PC, ID_EX_p21, ID_EX_p22, ID_EX_p23, ID_IR, ID_PC, ID_R1,
       ID_R2, IF_PC, LedData, MEM_PC, MEM_WB_memdata_2, multiplexer_1_out, multiplexer_5_out,
       multiplexer_7_out, multiplexer_8_out, multiplexer_11_out, multiplexer_12_out, multiplexer_13_out,
       PC_q, ram_1_data, rom_1_data, shifter_1_out, WB_ALU_Result, WB_PC, \无条件跳转地址 , \条件分支跳转地址 ;

  Button \u_总复位  (.out(RST));
  Button _1 (.out(IR1));
  Button _2 (.out(IR2));
  Button _3 (.out(IR3));
  Button \u_继续运行  (.out(Go));
  LED led_1 (.in(W1));
  LED led_2 (.in(W2));
  LED led_3 (.in(W3));
  Hex_Digit_Display hex_digit_display_1 (.value(LedData[31:28]));  // open: dp
  Comparator #(.width(32)) comparator_1 (.a(ID_R1), .b(32'h22), .eq(comparator_1_eq));  // open: gt, lt
  Hex_Digit_Display hex_digit_display_2 (.value(LedData[27:24]));  // open: dp
  Hex_Digit_Display hex_digit_display_3 (.value(LedData[23:20]));  // open: dp
  Multiplexer #(.select(2), .width(32), .enable("false")) multiplexer_1 (
    .in0(IF_PC), .in1(\无条件跳转地址 ), .in2(\条件分支跳转地址 ), .in3({32{1'b0}}), .out(multiplexer_1_out),
    .sel({Branch, JMP_out}));
  and and_1 (and_1_out, ~\数据相关 , EN);  // AND_Gate
  and and_2 (and_2_out, comparator_1_eq, Syscall);
  and and_3 (and_3_out, ~comparator_1_eq, Syscall);  // AND_Gate
  Hex_Digit_Display hex_digit_display_4 (.value(LedData[19:16]));  // open: dp
  Hex_Digit_Display hex_digit_display_5 (.value(LedData[15:12]));  // open: dp
  Adder #(.width(32)) adder_1 (.a(32'h4), .b(PC_q), .out(IF_PC));  // open: cin, cout
  Register #(.width(32)) PC (.D(multiplexer_1_out), .en(and_1_out), .Q(PC_q), .clk(CLK), .clr(RST));
  Register #(.width(32)) register_1 (.D(ID_R2), .en(and_2_out), .Q(LedData), .clk(CLK), .clr(RST));
  and and_4 (Halt, and_3_out, ~Go);  // AND_Gate
  Hex_Digit_Display hex_digit_display_6 (.value(LedData[7:4]));  // open: dp
  Hex_Digit_Display hex_digit_display_7 (.value(LedData[11:8]));  // open: dp
  Clock clock_1 (.out(CLK));
  not not_1 (EN, Halt);
  Hex_Digit_Display hex_digit_display_8 (.value(LedData[3:0]));  // open: dp
  ROM #(.addrWidth(10), .dataWidth(32)) rom_1 (.addr(PC_q[11:2]), .data(rom_1_data));  // open: sel
  or or_1 (or_1_out, Halt, \数据相关 );
  IF_ID IF_ID (
    .PC_in(IF_PC), .Instruction_in(rom_1_data), .PC_out(ID_PC), .Instruction_out(ID_IR),
    .\同步清零端_高电平有效 (\清零 ), .\使能端_低电平有效 (or_1_out), .CLK(CLK), .Reset(RST));
  Counter #(.width(16), .max('hffff)) counter_1 (
    .count(\暂停 ), .Q(\总周期数 ), .clk(CLK), .clr(RST));  // open: load, D, carry
  // Probe on \总周期数 
  // Probe on \无条件分支数 
  // Probe on \条件分支成功数 
  // Probe on \插入气泡数 
  // Probe on \LoadUse次数 
  // Probe on IF_PC[11:0]
  \数据相关检测  \u_数据相关检测_1  (
    .OP(ID_IR[31:26]), .EX_WriteReg_num(EX_WriteReg_num), .EX_RegWrite(EX_RegWrite),
    .MEM_WriteReg_num(MEM_WriteReg_num), .MEM_RegWrite(MEM_RegWrite), .\数据相关 (\数据相关 ), .Func(ID_IR[5:0]),
    .ID_R1_num(ID_R1_num), .ID_R2_num(ID_R2_num));  // open: foward_A, forward_B
  Multiplexer #(.width(5), .enable("false")) multiplexer_2 (
    .in0(ID_IR[25:21]), .in1(5'b00010), .out(ID_R1_num), .sel(Syscall));
  Multiplexer #(.width(5), .enable("false")) multiplexer_3 (
    .in0(ID_IR[20:16]), .in1(5'b00100), .out(ID_R2_num), .sel(Syscall));
  assign bit_extender_1_out = {{16{1'b0}}, ID_IR[15:0]};  // Bit_Extender bit_extender_1
  assign bit_extender_2_out = {{16{ID_IR[15]}}, ID_IR[15:0]};  // Bit_Extender bit_extender_2
  Counter #(.width(16), .max('hffff)) counter_2 (
    .count(and_5_out), .Q(\插入气泡数 ), .clk(CLK), .clr(RST));  // open: load, D, carry
  and and_5 (and_5_out, \数据相关 , \暂停 );
  // Probe on ID_PC[11:0]
  Multiplexer #(.width(5), .enable("false")) multiplexer_4 (
    .in0(ID_IR[20:16]), .in1(ID_IR[15:11]), .out(multiplexer_4_out), .sel(RegDst));
  Multiplexer #(.width(32), .enable("false")) multiplexer_5 (
    .in0(bit_extender_1_out), .in1(bit_extender_2_out), .out(multiplexer_5_out), .sel(SignedExt));
  // Probe on EX_PC[11:0]
  // Probe on MEM_PC[11:0]
  Multiplexer #(.width(5), .enable("false")) multiplexer_6 (
    .in0(multiplexer_4_out), .in1({5{1'b1}}), .out(multiplexer_6_out), .sel(JAL));
  // Probe on WB_PC[11:0]
  \硬布线控制器  \u_硬布线控制器_1  (
    .Func(ID_IR[5:0]), .OP(ID_IR[31:26]), .ALU_OP(Alu_op), .MemToReg(MemToReg), .MemWrite(MemWrite),
    .ALU_SRC(Alu_srcB), .RegWrite(RegWrite), .SysCALL(Syscall), .SignedExt(SignedExt), .RegDst(RegDst),
    .JR(EX[8]), .JMP(EX[9]), .Beq(Beq), .JAL(JAL), .Bne(Bne), .LHU(LHU), .BGEZ(BGEZ), .SLTIU(SLTIU),
    .SRAV(EX[10]));
  MIPS_Regifile mips_regifile_1 (
    .Din(Din), .Clk(CLK), .R1(ID_R1), .R2(ID_R2), .WE(WB_RegWrite), .W_num(MEM_WB_w_num_2),
    .R1_num(ID_R1_num), .R2_num(ID_R2_num));
  and and_6 (and_6_out, Branch, \暂停 );
  or or_2 (\清零 , Branch, JMP_out);
  Counter #(.width(16), .max('hffff)) counter_3 (
    .count(and_6_out), .Q(\条件分支成功数 ), .clk(CLK), .clr(RST));  // open: load, D, carry
  or or_3 (or_3_out, \数据相关 , \清零 );
  // ID_EX ID_EX: pin names not known; wires that end beside it: {LHU, SLTIU, JAL, Halt, MemToReg, RegWrite}, MemWrite, {EX, BGEZ, Bne, Beq, Alu_srcB, Alu_op}, ID_PC, ID_IR, ID_R1, ID_R2, multiplexer_5_out, ID_IR[10:6], multiplexer_6_out, or_3_out, ID_EX_p12, ID_EX_p12, CLK, RST, {ID_EX_p16, EX_RegWrite}, ID_EX_p17, {ID_EX_p18[10], JMP_out, JR_out, ID_EX_p18[7:0]}, EX_PC, EX_IR, ID_EX_p21, ID_EX_p22, ID_EX_p23, ID_EX_p24, EX_WriteReg_num
  Multiplexer #(.width(32), .enable("false")) multiplexer_7 (
    .in0(ID_EX_p22), .in1(ID_EX_p23), .out(multiplexer_7_out), .sel(ID_EX_p18[4]));
  Multiplexer #(.width(32), .enable("false")) multiplexer_8 (
    .in0(multiplexer_7_out), .in1({32{1'b0}}), .out(multiplexer_8_out), .sel(ID_EX_p18[7]));
  Shifter #(.width(32)) shifter_1 (.in(ID_EX_p23), .\dist (5'b00010), .out(shifter_1_out));
  Counter #(.width(16), .max('hffff)) counter_4 (
    .count(and_7_out), .Q(\无条件分支数 ), .clk(CLK), .clr(RST));  // open: load, D, carry
  and and_7 (and_7_out, JMP_out, \暂停 );
  and and_8 (and_8_out, ID_EX_p18[7], ~EX_ALU_Result[0]);  // AND_Gate
  and and_9 (and_9_out, ID_EX_p18[5], mips_alu_1_equal);
  and and_10 (and_10_out, ID_EX_p18[6], ~mips_alu_1_equal);  // AND_Gate
  MIPS_ALU mips_alu_1 (
    .X(ID_EX_p21), .Y(multiplexer_8_out), .AluOP(ID_EX_p18[3:0]), .Equal(mips_alu_1_equal),
    .Result(EX_ALU_Result), .shamt(multiplexer_9_out));  // open: Result_2
  Multiplexer #(.width(5), .enable("false")) multiplexer_9 (
    .in0(ID_EX_p24), .in1(ID_EX_p21[4:0]), .out(multiplexer_9_out), .sel(ID_EX_p18[10]));
  Adder #(.width(32)) adder_2 (.a(shifter_1_out), .b(EX_PC), .out(\条件分支跳转地址 ));  // open: cin, cout
  Multiplexer #(.width(32), .enable("false")) multiplexer_10 (
    .in0({EX_PC[31:28], EX_IR[25:0], 2'b00}), .in1(ID_EX_p21), .out(\无条件跳转地址 ), .sel(JR_out));
  or or_4 (Branch, and_9_out, and_8_out, and_10_out);
  EX_MEM EX_MEM (
    .MemWrite(ID_EX_p17), .PC_in(EX_PC), .Instruction_in(EX_IR), .B(ID_EX_p22), .Alu_result(EX_ALU_Result),
    .MemWrite_2(EX_MEM_memwrite_2), .PC_out(MEM_PC), .Instruction_out(EX_MEM_instruction_out),
    .B_2(EX_MEM_b_2), .Alu_result_2(EX_MEM_alu_result_2), .CLK(CLK), .W_num(EX_WriteReg_num),
    .W_num_2(MEM_WriteReg_num), .WB({ID_EX_p16, EX_RegWrite}), .WB_2({EX_MEM_wb_2, MEM_RegWrite}), .Reset(RST));  // open: 同步清零端_高电平有效, 使能端_低电平有效, A, A_2
  RAM #(.addrWidth(10), .dataWidth(32), .bus("separate")) ram_1 (
    .addr(EX_MEM_alu_result_2[11:2]), .din(EX_MEM_b_2), .data(ram_1_data), .str(EX_MEM_memwrite_2),
    .clk(CLK), .ld(not_2_out), .clr(RST));  // open: sel
  not not_2 (not_2_out, EX_MEM_memwrite_2);
  MEM_WB MEM_WB (
    .PC_in(MEM_PC), .Instruction_in(EX_MEM_instruction_out), .Alu_result(EX_MEM_alu_result_2),
    .MemData(ram_1_data), .PC_out(WB_PC), .Alu_result_2(WB_ALU_Result), .MemData_2(MEM_WB_memdata_2),
    .CLK(CLK), .W_num(MEM_WriteReg_num), .W_num_2(MEM_WB_w_num_2), .WB({EX_MEM_wb_2, MEM_RegWrite}),
    .WB_2({WB_LHU, WB_SLTIU, WB_JAL, MEM_WB_wb_2, WB_RegWrite}), .Reset(RST));  // open: Instruction_out, 同步清零端_高电平有效, 使能端_低电平有效, A, A_2, B, B_2
  Multiplexer #(.width(32), .enable("false")) multiplexer_11 (
    .in0(WB_ALU_Result), .in1(MEM_WB_memdata_2), .out(multiplexer_11_out), .sel(MEM_WB_wb_2[1]));
  not not_3 (\暂停 , MEM_WB_wb_2[2]);
  Multiplexer #(.width(32), .enable("false")) multiplexer_12 (
    .in0(multiplexer_11_out), .in1(WB_PC), .out(multiplexer_12_out), .sel(WB_JAL));
  Multiplexer #(.width(32), .enable("false")) multiplexer_13 (
    .in0({{16{1'b0}}, multiplexer_11_out[15:0]}), .in1({{16{1'b0}}, multiplexer_11_out[31:16]}),
    .out(multiplexer_13_out), .sel(WB_ALU_Result[1]));
  Multiplexer #(.select(2), .width(32), .enable("false")) multiplexer_14 (
    .in0(multiplexer_12_out), .in1(WB_ALU_Result), .in2(multiplexer_13_out), .in3({32{1'b0}}), .out(Din),
    .sel({WB_LHU, WB_SLTIU}));

  // Other names for the same wires on the sheet: EX[7:0] = {BGEZ, Bne, Beq, Alu_srcB, Alu_op}; JR = EX[8];
  //   JMP = EX[9]; SRAV = EX[10]; PCSel[1:0] = {Branch, JMP_out};
  //   WB[5:0] = {LHU, SLTIU, JAL, Halt, MemToReg, RegWrite}

  // Notes on the sheet:
  //   中断源
  //   中断等待指示
  //   数码管输出
  //   指令存储器
  //   contents of rom_1 (hex, n*v repeats v):
  //   20110004 ae310000 8e320000 2252fffc 20100000 22110001 2118020 22520004 ae500000 22310001 2118020
  //   22520004 ae500000 22310001 2118020 22520004 ae500000 22310001 2118020 22520004 ae500000 22310001
  //   2118020 22520004 ae500000 22310001 2118020 22520004 ae500000 22310001 2118020 22520004 ae500000
  //   2002000a 20100000 20100000 20100000 c
  //   指令字
  //   OP
  //   rs
  //   rt
  //   rd
  //   imm
  //   流水调试日志用
  //   OP
  //   Func
  //   插入气泡
  //   Alu_op
  //   Alu_src
  //   Beq
  //   Bne
  //   BGEZ
  //   JR
  //   JMP
  //   SRAV
  //   MemToReg
  //   半字片选
endmodule

module \重定向流水线  (
);

  wire Alu_srcB, and_1_out, and_2_out, and_3_out, and_4_out, and_5_out, and_6_out, and_7_out, and_8_out,
       and_9_out, and_10_out, and_11_out, Beq, BGEZ, Bne, Branch, CLK, comparator_2_eq, comparator_3_eq,
       comparator_4_eq, comparator_5_eq, comparator_6_eq, EN, EX_Load_Use, EX_MEM_memwrite_2, EX_MemToReg,
       EX_RegWrite, Go, Halt, ID_EX_memwrite_2, IR1, IR2, IR3, JAL, JMP_out, JR_out, LHU, Load_Use,
       MEM_RegWrite, MemToReg, MemWrite, mips_alu_1_equal, mips_probe_1_p1, not_1_out, or_1_out, or_4_out,
       R1_Used, R2_Used, RegDst, RegWrite, RST, SignedExt, SLTIU, Syscall, W1, W2, W3, WB_JAL, WB_LHU,
       WB_RegWrite, WB_SLTIU, WB_Sys, \数据相关 , \清零 ;
  wire [1:0] forward_A, forward_A_out, forward_B, ID_EX_forward_b_2, multiplexer_11_out, multiplexer_14_out;
  wire [1:1] MEM_WB_wb_2;
  wire [3:0] Alu_op;
  wire [4:0] EX_WriteReg_num, ID_EX_shmat_2, ID_R1_num, ID_R2_num, MEM_WB_w_num_2, MEM_WriteReg_num,
       multiplexer_4_out, multiplexer_6_out, multiplexer_9_out;
  wire [5:1] EX_MEM_wb_2;
  wire [5:2] ID_EX_wb_2;
  wire [10:0] ID_EX_ex_2;
  wire [10:8] EX;
  wire [15:0] \LoadUse次数 , \总周期数 , \无条件分支数 , \条件分支成功数 ;
  wire [31:0] bit_extender_1_out, bit_extender_2_out, Din, EX_ALU_Result, EX_IR, EX_MEM_a_2, EX_MEM_b_2,
       EX_MEM_instruction_out, EX_PC, ID_EX_a, ID_EX_b, ID_EX_imm_out, ID_IR, ID_PC, ID_R1, ID_R2, IF_PC,
       LedData, MEM_Alu_result, MEM_PC, multiplexer_1_out, multiplexer_5_out, multiplexer_7_out,
       multiplexer_8_out, multiplexer_12_out, multiplexer_13_out, multiplexer_15_out, multiplexer_16_out,
       multiplexer_17_out, PC_q, ram_1_data, rom_1_data, shifter_1_out, WB_ALU_Result, WB_memdata, WB_PC,
       WB_R1, WB_R2, \无条件跳转地址 , \条件分支跳转地址 ;

  Button \u_总复位  (.out(RST));
  Button _1 (.out(IR1));
  Button _2 (.out(IR2));
  Button _3 (.out(IR3));
  Button \u_继续运行  (.out(Go));
  LED led_1 (.in(W1));
  LED led_2 (.in(W2));
  LED led_3 (.in(W3));
  Comparator #(.width(5)) comparator_1 (.a(ID_R2_num), .b({5{1'b0}}));  // open: gt, eq, lt
  Hex_Digit_Display hex_digit_display_1 (.value(LedData[31:28]));  // open: dp
  Hex_Digit_Display hex_digit_display_2 (.value(LedData[23:20]));  // open: dp
  Hex_Digit_Display hex_digit_display_3 (.value(LedData[27:24]));  // open: dp
  Multiplexer #(.select(2), .width(32), .enable("false")) multiplexer_1 (
    .in0(IF_PC), .in1(\无条件跳转地址 ), .in2(\条件分支跳转地址 ), .in3({32{1'b0}}), .out(multiplexer_1_out),
    .sel({Branch, JMP_out}));
  and and_1 (and_1_out, ~Load_Use, EN);  // AND_Gate
  Hex_Digit_Display hex_digit_display_4 (.value(LedData[15:12]));  // open: dp
  Hex_Digit_Display hex_digit_display_5 (.value(LedData[19:16]));  // open: dp
  Comparator #(.width(5)) comparator_2 (.a(ID_R1_num), .b({5{1'b0}}), .eq(comparator_2_eq));  // open: gt, lt
  Comparator #(.width(5)) comparator_3 (.a(EX_WriteReg_num), .b(ID_R1_num), .eq(comparator_3_eq));  // open: gt, lt
  Comparator #(.width(5)) comparator_4 (.a(ID_R2_num), .b({5{1'b0}}), .eq(comparator_4_eq));  // open: gt, lt
  Comparator #(.width(5)) comparator_5 (.a(EX_WriteReg_num), .b(ID_R2_num), .eq(comparator_5_eq));  // open: gt, lt
  Register #(.width(32)) PC (.D(multiplexer_1_out), .en(and_1_out), .Q(PC_q), .clk(CLK), .clr(RST));
  Hex_Digit_Display hex_digit_display_6 (.value(LedData[11:8]));  // open: dp
  Hex_Digit_Display hex_digit_display_7 (.value(LedData[7:4]));  // open: dp
  Clock clock_1 (.out(CLK));
  Adder #(.width(32)) adder_1 (.a(32'h4), .b(PC_q), .out(IF_PC));  // open: cin, cout
  Hex_Digit_Display hex_digit_display_8 (.value(LedData[3:0]));  // open: dp
  and and_2 (and_2_out, ~comparator_2_eq, EX_MemToReg, R1_Used, comparator_3_eq);  // AND_Gate
  and and_3 (and_3_out, ~comparator_4_eq, R2_Used, EX_MemToReg, comparator_5_eq);  // AND_Gate
  ROM #(.addrWidth(10), .dataWidth(32)) rom_1 (.addr(PC_q[11:2]), .data(rom_1_data));  // open: sel
  or or_1 (or_1_out, Halt, Load_Use);
  or or_2 (Load_Use, and_2_out, and_3_out);
  IF_ID IF_ID (
    .PC_in(IF_PC), .Instruction_in(rom_1_data), .PC_out(ID_PC), .Instruction_out(ID_IR),
    .\同步清零端_高电平有效 (\清零 ), .\使能端_低电平有效 (or_1_out), .CLK(CLK), .Reset(RST));
  Counter #(.width(16), .max('hffff)) counter_1 (.count(EN), .Q(\总周期数 ), .clk(CLK), .clr(RST));  // open: load, D, carry
  // Probe on \总周期数 
  // Probe on \无条件分支数 
  // Probe on \条件分支成功数 
  // Probe on \LoadUse次数 
  // Probe on \LoadUse次数 
  // Probe on IF_PC[11:0]
  \数据相关检测  \u_数据相关检测_1  (
    .OP(ID_IR[31:26]), .EX_WriteReg_num(EX_WriteReg_num), .EX_RegWrite(EX_RegWrite),
    .MEM_WriteReg_num(MEM_WriteReg_num), .MEM_RegWrite(MEM_RegWrite), .\数据相关 (\数据相关 ), .Func(ID_IR[5:0]),
    .ID_R1_num(ID_R1_num), .ID_R2_num(ID_R2_num), .foward_A(forward_A), .forward_B(forward_B));
  Multiplexer #(.width(5), .enable("false")) multiplexer_2 (
    .in0(ID_IR[25:21]), .in1(5'b00010), .out(ID_R1_num), .sel(Syscall));
  Multiplexer #(.width(5), .enable("false")) multiplexer_3 (
    .in0(ID_IR[20:16]), .in1(5'b00100), .out(ID_R2_num), .sel(Syscall));
  assign bit_extender_1_out = {{16{1'b0}}, ID_IR[15:0]};  // Bit_Extender bit_extender_1
  assign bit_extender_2_out = {{16{ID_IR[15]}}, ID_IR[15:0]};  // Bit_Extender bit_extender_2
  and and_4 (and_4_out, Load_Use, EN);
  // Probe on ID_PC[11:0]
  \源寄存器使用情况  \u_源寄存器使用情况_1  (
    .OP0(ID_IR[26]), .OP1(ID_IR[27]), .OP2(ID_IR[28]), .OP3(ID_IR[29]), .OP4(ID_IR[30]), .OP5(ID_IR[31]),
    .F0(ID_IR[0]), .F1(ID_IR[1]), .F2(ID_IR[2]), .F3(ID_IR[3]), .F4(ID_IR[4]), .F5(ID_IR[5]),
    .R1_Used(R1_Used), .R2_Used(R2_Used));
  Multiplexer #(.width(5), .enable("false")) multiplexer_4 (
    .in0(ID_IR[20:16]), .in1(ID_IR[15:11]), .out(multiplexer_4_out), .sel(RegDst));
  Multiplexer #(.width(32), .enable("false")) multiplexer_5 (
    .in0(bit_extender_1_out), .in1(bit_extender_2_out), .out(multiplexer_5_out), .sel(SignedExt));
  Counter #(.width(16), .max('hffff)) counter_2 (
    .count(and_4_out), .Q(\LoadUse次数 ), .clk(CLK), .clr(RST));  // open: load, D, carry
  // Probe on EX_PC[11:0]
  // Probe on MEM_PC[11:0]
  Multiplexer #(.width(5), .enable("false")) multiplexer_6 (
    .in0(multiplexer_4_out), .in1({5{1'b1}}), .out(multiplexer_6_out), .sel(JAL));
  // Probe on WB_PC[11:0]
  \硬布线控制器  \u_硬布线控制器_1  (
    .Func(ID_IR[5:0]), .OP(ID_IR[31:26]), .ALU_OP(Alu_op), .MemToReg(MemToReg), .MemWrite(MemWrite),
    .ALU_SRC(Alu_srcB), .RegWrite(RegWrite), .SysCALL(Syscall), .SignedExt(SignedExt), .RegDst(RegDst),
    .JR(EX[8]), .JMP(EX[9]), .Beq(Beq), .JAL(JAL), .Bne(Bne), .LHU(LHU), .BGEZ(BGEZ), .SLTIU(SLTIU),
    .SRAV(EX[10]));
  MIPS_Regifile mips_regifile_1 (
    .Din(Din), .Clk(CLK), .R1(ID_R1), .R2(ID_R2), .WE(WB_RegWrite), .W_num(MEM_WB_w_num_2),
    .R1_num(ID_R1_num), .R2_num(ID_R2_num));
  or or_3 (\清零 , Branch, JMP_out);
  Counter #(.width(16), .max('hffff)) counter_3 (
    .count(and_5_out), .Q(\条件分支成功数 ), .clk(CLK), .clr(RST));  // open: load, D, carry
  and and_5 (and_5_out, Branch, EN);
  or or_4 (or_4_out, Load_Use, \清零 );
  ID_EX ID_EX (
    .PC_in(ID_PC), .Instruction_in(ID_IR), .RD1(ID_R1), .RD2(ID_R2), .imm_in(multiplexer_5_out),
    .PC_out(EX_PC), .Instruction_out(EX_IR), .A(ID_EX_a), .B(ID_EX_b), .imm_out(ID_EX_imm_out),
    .\同步清零端_高电平有效 (or_4_out), .\使能端_低电平有效 (Halt), .CLK(CLK), .shmat(ID_IR[10:6]), .shmat_2(ID_EX_shmat_2),
    .W_num(multiplexer_6_out), .W_num_2(EX_WriteReg_num), .EX({EX, BGEZ, Bne, Beq, Alu_srcB, Alu_op}),
    .EX_2({ID_EX_ex_2[10], JMP_out, JR_out, ID_EX_ex_2[7:0]}),
    .WB({LHU, SLTIU, JAL, Syscall, MemToReg, RegWrite}), .WB_2({ID_EX_wb_2, EX_MemToReg, EX_RegWrite}),
    .MemWrite(MemWrite), .MemWrite_2(ID_EX_memwrite_2), .Reset(RST), .forward_A(forward_A),
    .forward_B(forward_B), .forward_A_2(forward_A_out), .forward_B_2(ID_EX_forward_b_2), .Load_Use(Load_Use),
    .Load_use_2(EX_Load_Use));
  Multiplexer #(.width(32), .enable("false")) multiplexer_7 (
    .in0(multiplexer_13_out), .in1(ID_EX_imm_out), .out(multiplexer_7_out), .sel(ID_EX_ex_2[4]));
  Multiplexer #(.width(32), .enable("false")) multiplexer_8 (
    .in0(multiplexer_7_out), .in1({32{1'b0}}), .out(multiplexer_8_out), .sel(ID_EX_ex_2[7]));
  Shifter #(.width(32)) shifter_1 (.in(ID_EX_imm_out), .\dist (5'b00010), .out(shifter_1_out));
  // Mips_Probe mips_probe_1: pin names not known; wires that end beside it: mips_probe_1_p1, mips_probe_1_p1, EX_IR
  and and_6 (and_6_out, JMP_out, EN);
  and and_7 (and_7_out, ID_EX_ex_2[7], ~EX_ALU_Result[0]);  // AND_Gate
  and and_8 (and_8_out, ID_EX_ex_2[5], mips_alu_1_equal);
  and and_9 (and_9_out, ID_EX_ex_2[6], ~mips_alu_1_equal);  // AND_Gate
  Multiplexer #(.width(5), .enable("false")) multiplexer_9 (
    .in0(ID_EX_shmat_2), .in1(ID_EX_a[4:0]), .out(multiplexer_9_out), .sel(ID_EX_ex_2[10]));
  Adder #(.width(32)) adder_2 (.a(shifter_1_out), .b(EX_PC), .out(\条件分支跳转地址 ));  // open: cin, cout
  Multiplexer #(.width(32), .enable("false")) multiplexer_10 (
    .in0({EX_PC[31:28], EX_IR[25:0], 2'b00}), .in1(ID_EX_a), .out(\无条件跳转地址 ), .sel(JR_out));
  Counter #(.width(16), .max('hffff)) counter_4 (
    .count(and_6_out), .Q(\无条件分支数 ), .clk(CLK), .clr(RST));  // open: load, D, carry
  or or_5 (Branch, and_8_out, and_7_out, and_9_out);
  Multiplexer #(.width(2), .enable("false")) multiplexer_11 (
    .in0(forward_A_out), .in1(2'b00), .out(multiplexer_11_out), .sel(EX_Load_Use));
  Multiplexer #(.select(2), .width(32), .enable("false")) multiplexer_12 (
    .in0(ID_EX_a), .in1(Din), .in2(MEM_Alu_result), .in3(MEM_Alu_result), .out(multiplexer_12_out),
    .sel(multiplexer_11_out));
  Multiplexer #(.select(2), .width(32), .enable("false")) multiplexer_13 (
    .in0(ID_EX_b), .in1(Din), .in2(MEM_Alu_result), .in3(MEM_Alu_result), .out(multiplexer_13_out),
    .sel(multiplexer_14_out));
  Multiplexer #(.width(2), .enable("false")) multiplexer_14 (
    .in0(ID_EX_forward_b_2), .in1(2'b00), .out(multiplexer_14_out), .sel(EX_Load_Use));
  MIPS_ALU mips_alu_1 (
    .X(multiplexer_12_out), .Y(multiplexer_8_out), .AluOP(ID_EX_ex_2[3:0]), .Equal(mips_alu_1_equal),
    .Result(EX_ALU_Result), .shamt(multiplexer_9_out));  // open: Result_2
  EX_MEM EX_MEM (
    .MemWrite(ID_EX_memwrite_2), .PC_in(EX_PC), .Instruction_in(EX_IR), .B(multiplexer_13_out),
    .Alu_result(EX_ALU_Result), .MemWrite_2(EX_MEM_memwrite_2), .PC_out(MEM_PC),
    .Instruction_out(EX_MEM_instruction_out), .B_2(EX_MEM_b_2), .Alu_result_2(MEM_Alu_result),
    .\使能端_低电平有效 (Halt), .CLK(CLK), .W_num(EX_WriteReg_num), .W_num_2(MEM_WriteReg_num),
    .WB({ID_EX_wb_2, EX_MemToReg, EX_RegWrite}), .WB_2({EX_MEM_wb_2, MEM_RegWrite}), .Reset(RST),
    .A(multiplexer_12_out), .A_2(EX_MEM_a_2));  // open: 同步清零端_高电平有效
  RAM #(.addrWidth(10), .dataWidth(32), .bus("separate")) ram_1 (
    .addr(MEM_Alu_result[11:2]), .din(EX_MEM_b_2), .data(ram_1_data), .str(EX_MEM_memwrite_2), .clk(CLK),
    .ld(not_1_out), .clr(RST));  // open: sel
  not not_1 (not_1_out, EX_MEM_memwrite_2);
  MEM_WB MEM_WB (
    .PC_in(MEM_PC), .Instruction_in(EX_MEM_instruction_out), .Alu_result(MEM_Alu_result),
    .MemData(ram_1_data), .PC_out(WB_PC), .Alu_result_2(WB_ALU_Result), .MemData_2(WB_memdata),
    .\使能端_低电平有效 (Halt), .CLK(CLK), .W_num(MEM_WriteReg_num), .W_num_2(MEM_WB_w_num_2),
    .WB({EX_MEM_wb_2, MEM_RegWrite}), .WB_2({WB_LHU, WB_SLTIU, WB_JAL, WB_Sys, MEM_WB_wb_2[1], WB_RegWrite}),
    .Reset(RST), .A(EX_MEM_a_2), .A_2(WB_R1), .B(EX_MEM_b_2), .B_2(WB_R2));  // open: Instruction_out, 同步清零端_高电平有效
  Comparator #(.width(32)) comparator_6 (.a(WB_R1), .b(32'h22), .eq(comparator_6_eq));  // open: gt, lt
  Multiplexer #(.width(32), .enable("false")) multiplexer_15 (
    .in0(WB_ALU_Result), .in1(WB_memdata), .out(multiplexer_15_out), .sel(MEM_WB_wb_2[1]));
  and and_10 (and_10_out, comparator_6_eq, WB_Sys);
  and and_11 (and_11_out, ~comparator_6_eq, WB_Sys);  // AND_Gate
  Multiplexer #(.width(32), .enable("false")) multiplexer_16 (
    .in0(multiplexer_15_out), .in1(WB_PC), .out(multiplexer_16_out), .sel(WB_JAL));
  Register #(.width(32)) register_1 (.D(WB_R2), .en(and_10_out), .Q(LedData), .clk(CLK), .clr(RST));
  and and_12 (Halt, and_11_out, ~Go);  // AND_Gate
  not not_2 (EN, Halt);
  Multiplexer #(.width(32), .enable("false")) multiplexer_17 (
    .in0({{16{1'b0}}, multiplexer_15_out[15:0]}), .in1({{16{1'b0}}, multiplexer_15_out[31:16]}),
    .out(multiplexer_17_out), .sel(WB_ALU_Result[1]));
  Multiplexer #(.select(2), .width(32), .enable("false")) multiplexer_18 (
    .in0(multiplexer_16_out), .in1(WB_ALU_Result), .in2(multiplexer_17_out), .in3({32{1'b0}}), .out(Din),
    .sel({WB_LHU, WB_SLTIU}));

  // Other names for the same wires on the sheet: EX[7:0] = {BGEZ, Bne, Beq, Alu_srcB, Alu_op}; JR = EX[8];
  //   JMP = EX[9]; SRAV = EX[10]; PCSel[1:0] = {Branch, JMP_out};
  //   WB[5:0] = {LHU, SLTIU, JAL, Syscall, MemToReg, RegWrite}; 插入气泡数[15:0] = \LoadUse次数 

  // Notes on the sheet:
  //   中断源
  //   中断等待指示
  //   数码管输出
  //   指令存储器
  //   contents of rom_1 (hex, n*v repeats v):
  //   20110001 8100005 20110001 20120002 20130003 8100009 20110001 20120002 20130003 810000d 20110001
  //   20120002 20130003 8100011 20110001 20120002 20130003 c1000f6 20100001 20110001 118fc0 112020
  //   20020022 c 118882 12200001 8100015 112020 20020022 c 20110001 118880 112020 20020022 c 12200001
  //   810001f 20110001 118fc0 112020 20020022 c 1188c3 112020 20020022 c 118903 112020 20020022 c 118903
  //   112020 20020022 c 118903 112020 20020022 c 118903 112020 20020022 c 118903 112020 20020022 c 118903
  //   112020 20020022 c 118903 112020 20020022 c 20100001 109fc0 139fc3 8021 2012000c 24160003 26100001
  //   3210000f 20080008 20090001 139900 2709825 132020 20020022 c 1094022 1500fff9 22100001 2018000f
  //   2188024 108700 20080008 20090001 139902 2709825 132021 20020022 c 1094022 1500fff9 108702 2c9b022
  //   12c00001 8100050 4020 1084027 84400 3508ffff 82021 20020022 c 2010ffff 20110000 ae300000 22100001
  //   22310004 ae300000 22100001 22310004 ae300000 22100001 22310004 ae300000 22100001 22310004 ae300000
  //   22100001 22310004 ae300000 22100001 22310004 ae300000 22100001 22310004 ae300000 22100001 22310004
  //   ae300000 22100001 22310004 ae300000 22100001 22310004 ae300000 22100001 22310004 ae300000 22100001
  //   22310004 ae300000 22100001 22310004 ae300000 22100001 22310004 ae300000 22100001 22310004 ae300000
  //   22100001 22310004 22100001 8020 2011003c 8e130000 8e340000 274402a 11000002 ae330000 ae140000
  //   2231fffc 1611fff8 102020 20020022 c 22100004 2011003c 1611fff2 20020032 c 20080001 20090003 20110876
  //   118d00 112020 20020022 c 200b0008 1118807 1318807 112020 20020022 c 216bffff 1560fff9 2002000a c
  //   2008ffff 20090000 20111997 112020 20020022 c 2288820 2e291949 1120fffa 2002000a c 20090000 200b0010
  //   34118483 20120404 118c00 129400 36318281 22520404 ad310000 2328820 21290004 216bffff 1560fffb
  //   200b0020 20090000 95310000 112020 20020022 c 21290002 216bffff 1560fff9 2002000a c 2011000f 112020
  //   20020022 c 2231ffff 621fffb 2002000a c 2002000a c 20100000 22100001 102020 20020022 c 22100002
  //   102020 20020022 c 22100003 102020 20020022 c 22100004 102020 20020022 c 22100005 102020 20020022 c
  //   22100006 102020 20020022 c 22100007 102020 20020022 c 22100008 102020 20020022 20020022 c 3e00008
  //   OP
  //   rs
  //   指令字
  //   rt
  //   rd
  //   imm
  //   OP
  //   Func
  //   流水调试日志用
  //   插入气泡
  //   Alu_op
  //   Alu_src
  //   Beq
  //   Bne
  //   BGEZ
  //   JR
  //   JMP
  //   SRAV
  //   MemToReg
  //   半字片选
endmodule
